// Logisim project 2 HEX-Display.circ as structural Verilog: 6 circuits, main circuit main
module main (
  input  [7:0] in_1
);

  wire [2:0] main2_1_lb, main2_1_lb_2;
  wire [3:0] main2_1_m, main2_1_m_2;

  _7_Segment_Display u_7_segment_display_1 (
    .g(main2_1_m[0]), .f(main2_1_m[1]), .a(main2_1_m[2]), .b(main2_1_m[3]), .e(main2_1_lb[0]),
    .d(main2_1_lb[1]), .c(main2_1_lb[2]));  // open: dp
  _7_Segment_Display u_7_segment_display_2 (
    .g(main2_1_m_2[0]), .f(main2_1_m_2[1]), .a(main2_1_m_2[2]), .b(main2_1_m_2[3]), .e(main2_1_lb_2[0]),
    .d(main2_1_lb_2[1]), .c(main2_1_lb_2[2]));  // open: dp
  main2 main2_1 (
    .M(main2_1_m[0]), .LT(main2_1_m[1]), .T(main2_1_m[2]), .RT(main2_1_m[3]), .LB(main2_1_lb[0]),
    .B(main2_1_lb[1]), .RB(main2_1_lb[2]), .M_2(main2_1_m_2[0]), .LT_2(main2_1_m_2[1]), .T_2(main2_1_m_2[2]),
    .RT_2(main2_1_m_2[3]), .LB_2(main2_1_lb_2[0]), .B_2(main2_1_lb_2[1]), .RB_2(main2_1_lb_2[2]), .in_1(in_1));
endmodule

module _8b_Register (
  input  IN_1,
  input  IN_2,
  input  IN_3,
  input  IN_4,
  input  IN_5,
  input  IN_6,
  input  IN_7,
  input  IN_8,
  input  CLK,
  input  CU_Signal,
  output OUT_1,
  output OUT_2,
  output OUT_3,
  output OUT_4,
  output OUT_5,
  output OUT_6,
  output OUT_7,
  output OUT_8
);

  wire and_1_out;

  and and_1 (and_1_out, CLK, CU_Signal);
  D_Flip_Flop d_ff_1 (.clk(and_1_out), .D(IN_1), .Q(OUT_1));  // open: Qn, preset, en, reset
  D_Flip_Flop d_ff_2 (.clk(and_1_out), .D(IN_2), .Q(OUT_2));  // open: Qn, preset, en, reset
  D_Flip_Flop d_ff_3 (.clk(and_1_out), .D(IN_3), .Q(OUT_3));  // open: Qn, preset, en, reset
  D_Flip_Flop d_ff_4 (.clk(and_1_out), .D(IN_4), .Q(OUT_4));  // open: Qn, preset, en, reset
  D_Flip_Flop d_ff_5 (.clk(and_1_out), .D(IN_5), .Q(OUT_5));  // open: Qn, preset, en, reset
  D_Flip_Flop d_ff_6 (.clk(and_1_out), .D(IN_6), .Q(OUT_6));  // open: Qn, preset, en, reset
  D_Flip_Flop d_ff_7 (.clk(and_1_out), .D(IN_7), .Q(OUT_7));  // open: Qn, preset, en, reset
  D_Flip_Flop d_ff_8 (.clk(and_1_out), .D(IN_8), .Q(OUT_8));  // open: Qn, preset, en, reset
endmodule

module S2 (
  input  IN_1,
  input  IN_2,
  input  IN_3,
  input  IN_4,
  output OUT_15,
  output OUT_14,
  output OUT_13,
  output OUT_12,
  output OUT_11,
  output OUT_10,
  output OUT_9,
  output OUT_8,
  output OUT_7,
  output OUT_6,
  output OUT_5,
  output OUT_4,
  output OUT_3,
  output OUT_2,
  output OUT_1,
  output OUT_0
);

  wire not_1_out, not_2_out, not_3_out, not_4_out, not_5_out, not_6_out, not_7_out, not_8_out, not_9_out,
       not_10_out, not_11_out, not_12_out, not_13_out, not_14_out, not_15_out, not_16_out, not_17_out,
       not_18_out, not_19_out, not_20_out, not_21_out, not_22_out, not_23_out, not_24_out, not_25_out,
       not_26_out, not_27_out, not_28_out, not_29_out, not_30_out, not_31_out, not_32_out;

  and and_1 (OUT_15, IN_4, IN_3, IN_2, IN_1);
  and and_2 (OUT_14, IN_4, IN_3, IN_2, not_1_out);
  not not_1 (not_1_out, IN_1);
  and and_3 (OUT_13, IN_4, IN_3, not_2_out, IN_1);
  not not_2 (not_2_out, IN_2);
  and and_4 (OUT_12, IN_4, IN_3, not_3_out, not_4_out);
  not not_3 (not_3_out, IN_2);
  not not_4 (not_4_out, IN_1);
  and and_5 (OUT_11, IN_4, not_5_out, IN_2, IN_1);
  not not_5 (not_5_out, IN_3);
  and and_6 (OUT_10, IN_4, not_6_out, IN_2, not_7_out);
  not not_6 (not_6_out, IN_3);
  not not_7 (not_7_out, IN_1);
  and and_7 (OUT_9, IN_4, not_8_out, not_9_out, IN_1);
  not not_8 (not_8_out, IN_3);
  not not_9 (not_9_out, IN_2);
  and and_8 (OUT_8, IN_4, not_10_out, not_11_out, not_12_out);
  not not_10 (not_10_out, IN_3);
  not not_11 (not_11_out, IN_2);
  not not_12 (not_12_out, IN_1);
  and and_9 (OUT_7, not_13_out, IN_3, IN_2, IN_1);
  not not_13 (not_13_out, IN_4);
  and and_10 (OUT_6, not_14_out, IN_3, IN_2, not_15_out);
  and and_11 (OUT_5, not_16_out, IN_3, not_17_out, IN_1);
  not not_14 (not_14_out, IN_4);
  not not_15 (not_15_out, IN_1);
  not not_16 (not_16_out, IN_4);
  not not_17 (not_17_out, IN_2);
  and and_12 (OUT_4, not_18_out, IN_3, not_19_out, not_20_out);
  not not_18 (not_18_out, IN_4);
  not not_19 (not_19_out, IN_2);
  not not_20 (not_20_out, IN_1);
  and and_13 (OUT_3, not_21_out, not_22_out, IN_2, IN_1);
  and and_14 (OUT_2, not_23_out, not_24_out, IN_2, not_25_out);
  not not_21 (not_21_out, IN_4);
  not not_22 (not_22_out, IN_3);
  and and_15 (OUT_1, not_26_out, not_27_out, not_28_out, IN_1);
  and and_16 (OUT_0, not_29_out, not_30_out, not_31_out, not_32_out);
  not not_23 (not_23_out, IN_4);
  not not_24 (not_24_out, IN_3);
  not not_25 (not_25_out, IN_1);
  not not_26 (not_26_out, IN_4);
  not not_27 (not_27_out, IN_3);
  not not_28 (not_28_out, IN_2);
  not not_29 (not_29_out, IN_4);
  not not_30 (not_30_out, IN_3);
  not not_31 (not_31_out, IN_2);
  not not_32 (not_32_out, IN_1);

  // Notes on the sheet:
  //   AND 1111
  //   AND 1110
  //   AND 1101
  //   AND 1100
  //   AND 1011
  //   AND 1010
  //   AND 1001
  //   AND 1000
  //   AND 0111
  //   AND 0110
  //   AND 0101
  //   AND 0100
  //   AND 0011
  //   AND 0010
  //   AND 0001
  //   AND 0000
endmodule

module _7seg (
  input  IN_15,
  input  IN_14,
  input  IN_13,
  input  IN_12,
  input  IN_11,
  input  IN_10,
  input  IN_9,
  input  IN_8,
  input  IN_7,
  input  IN_6,
  input  IN_5,
  input  IN_4,
  input  IN_3,
  input  IN_2,
  input  IN_1,
  input  IN_0,
  output RT,
  output RB,
  output M,
  output T,
  output LB,
  output LT,
  output B
);

  or u_RT (RT, IN_13, IN_10, IN_9, IN_8, IN_7, IN_4, IN_3, IN_2, IN_1, IN_0);
  or u_RB (RB, IN_13, IN_11, IN_10, IN_9, IN_8, IN_7, IN_6, IN_5, IN_4, IN_3, IN_1, IN_0);
  or u_M (M, IN_15, IN_14, IN_13, IN_11, IN_10, IN_9, IN_8, IN_6, IN_5, IN_4, IN_3, IN_2);
  or u_T (T, IN_15, IN_14, IN_12, IN_10, IN_9, IN_8, IN_7, IN_6, IN_5, IN_3, IN_2, IN_0);
  ExactlyOne u_LB (
    .out(LB), .in0(IN_11), .in1(IN_15), .in2(IN_14), .in3(IN_13), .in4(IN_12), .in5(IN_10), .in6(IN_8),
    .in7(IN_6), .in8(IN_2), .in9(IN_0));
  or u_LT (LT, IN_15, IN_14, IN_12, IN_11, IN_10, IN_9, IN_8, IN_6, IN_5, IN_4, IN_0);
  or u_B (B, IN_14, IN_13, IN_12, IN_11, IN_9, IN_8, IN_6, IN_5, IN_3, IN_2, IN_0);
endmodule

module _7seg2 (
  input  IN_15,
  input  IN_14,
  input  IN_13,
  input  IN_12,
  input  IN_11,
  input  IN_10,
  input  IN_9,
  input  IN_8,
  input  IN_7,
  input  IN_6,
  input  IN_5,
  input  IN_4,
  input  IN_3,
  input  IN_2,
  input  IN_1,
  input  IN_0,
  output M,
  output LT,
  output T,
  output RT,
  output LB,
  output B,
  output RB
);

  or u_M (M, IN_15, IN_14, IN_13, IN_11, IN_10, IN_9, IN_8, IN_6, IN_5, IN_4, IN_3, IN_2);
  or u_LT (LT, IN_15, IN_14, IN_12, IN_11, IN_10, IN_9, IN_8, IN_6, IN_5, IN_4, IN_0);
  or u_T (T, IN_15, IN_14, IN_12, IN_10, IN_9, IN_8, IN_7, IN_6, IN_5, IN_3, IN_2, IN_0);
  or u_RT (RT, IN_13, IN_10, IN_9, IN_8, IN_7, IN_4, IN_3, IN_2, IN_1, IN_0);
  ExactlyOne u_LB (
    .out(LB), .in0(IN_15), .in1(IN_14), .in2(IN_13), .in3(IN_12), .in4(IN_11), .in5(IN_10), .in6(IN_8),
    .in7(IN_6), .in8(IN_2), .in9(IN_0));
  or u_B (B, IN_14, IN_13, IN_12, IN_11, IN_9, IN_8, IN_6, IN_5, IN_3, IN_2, IN_0);
  or u_RB (RB, IN_13, IN_11, IN_10, IN_9, IN_8, IN_7, IN_6, IN_5, IN_4, IN_3, IN_1, IN_0);
endmodule

module main2 (
  input  [7:0] in_1,
  output M,
  output LT,
  output T,
  output RT,
  output LB,
  output B,
  output RB,
  output M_2,
  output LT_2,
  output T_2,
  output RT_2,
  output LB_2,
  output B_2,
  output RB_2
);

  wire s2_1_out_0, s2_1_out_1, s2_1_out_2, s2_1_out_3, s2_1_out_4, s2_1_out_5, s2_1_out_6, s2_1_out_7,
       s2_1_out_8, s2_1_out_9, s2_1_out_10, s2_1_out_11, s2_1_out_12, s2_1_out_13, s2_1_out_14, s2_1_out_15,
       s2_2_out_0, s2_2_out_1, s2_2_out_2, s2_2_out_3, s2_2_out_4, s2_2_out_5, s2_2_out_6, s2_2_out_7,
       s2_2_out_8, s2_2_out_9, s2_2_out_10, s2_2_out_11, s2_2_out_12, s2_2_out_13, s2_2_out_14, s2_2_out_15;

  _7seg2 u_7seg2_1 (
    .M(M), .LT(LT), .T(T), .RT(RT), .LB(LB), .B(B), .RB(RB), .IN_15(s2_1_out_15), .IN_14(s2_1_out_14),
    .IN_13(s2_1_out_13), .IN_12(s2_1_out_12), .IN_11(s2_1_out_11), .IN_10(s2_1_out_10), .IN_9(s2_1_out_9),
    .IN_8(s2_1_out_8), .IN_7(s2_1_out_7), .IN_6(s2_1_out_6), .IN_5(s2_1_out_5), .IN_4(s2_1_out_4),
    .IN_3(s2_1_out_3), .IN_2(s2_1_out_2), .IN_1(s2_1_out_1), .IN_0(s2_1_out_0));
  _7seg2 u_7seg2_2 (
    .M(M_2), .LT(LT_2), .T(T_2), .RT(RT_2), .LB(LB_2), .B(B_2), .RB(RB_2), .IN_15(s2_2_out_15),
    .IN_14(s2_2_out_14), .IN_13(s2_2_out_13), .IN_12(s2_2_out_12), .IN_11(s2_2_out_11), .IN_10(s2_2_out_10),
    .IN_9(s2_2_out_9), .IN_8(s2_2_out_8), .IN_7(s2_2_out_7), .IN_6(s2_2_out_6), .IN_5(s2_2_out_5),
    .IN_4(s2_2_out_4), .IN_3(s2_2_out_3), .IN_2(s2_2_out_2), .IN_1(s2_2_out_1), .IN_0(s2_2_out_0));
  S2 s2_1 (
    .OUT_15(s2_1_out_15), .OUT_14(s2_1_out_14), .OUT_13(s2_1_out_13), .OUT_12(s2_1_out_12),
    .OUT_11(s2_1_out_11), .OUT_10(s2_1_out_10), .OUT_9(s2_1_out_9), .OUT_8(s2_1_out_8), .OUT_7(s2_1_out_7),
    .OUT_6(s2_1_out_6), .OUT_5(s2_1_out_5), .OUT_4(s2_1_out_4), .OUT_3(s2_1_out_3), .OUT_2(s2_1_out_2),
    .OUT_1(s2_1_out_1), .OUT_0(s2_1_out_0), .IN_1(in_1[0]), .IN_2(in_1[1]), .IN_3(in_1[2]), .IN_4(in_1[3]));
  S2 s2_2 (
    .OUT_15(s2_2_out_15), .OUT_14(s2_2_out_14), .OUT_13(s2_2_out_13), .OUT_12(s2_2_out_12),
    .OUT_11(s2_2_out_11), .OUT_10(s2_2_out_10), .OUT_9(s2_2_out_9), .OUT_8(s2_2_out_8), .OUT_7(s2_2_out_7),
    .OUT_6(s2_2_out_6), .OUT_5(s2_2_out_5), .OUT_4(s2_2_out_4), .OUT_3(s2_2_out_3), .OUT_2(s2_2_out_2),
    .OUT_1(s2_2_out_1), .OUT_0(s2_2_out_0), .IN_1(in_1[4]), .IN_2(in_1[5]), .IN_3(in_1[6]), .IN_4(in_1[7]));
endmodule
