// Logisim project 8bitALU.circ as structural Verilog: 10 circuits, main circuit 8bitALU
// ALU
module _8bitALU (
  input  add_sub,
  input  mult,
  input  Input_A0,
  input  Input_A1,
  input  Input_A2,
  input  Input_A3,
  input  Input_A4,
  input  Input_A5,
  input  Input_A6,
  input  Input_A7,
  input  Input_B0,
  input  Input_B1,
  input  Input_B2,
  input  Input_B3,
  input  Input_B4,
  input  Input_B5,
  input  Input_B6,
  input  Input_B7,
  output Output_0,
  output Output_1,
  output Output_2,
  output Output_3,
  output Output_4,
  output Output_5,
  output Output_6,
  output Output_7,
  output Overflow,
  output Zero
);

  wire and_1_out, and_2_out, and_3_out, and_4_out, and_5_out, and_6_out, and_7_out, and_8_out, and_9_out,
       and_10_out, and_11_out, and_12_out, and_13_out, and_14_out, and_15_out, and_16_out, and_17_out,
       and_18_out, n1bitadder_0_1_carry_out, n1bitadder_0_1_result, n1bitadder_0_2_carry_out,
       n1bitadder_0_2_result, n1bitadder_1_carry_out, n1bitadder_1_result, n1bitadder_2_carry_out,
       n1bitadder_2_result, n1bitadder_3_carry_out, n1bitadder_3_result, n1bitadder_4_carry_out,
       n1bitadder_4_result, n1bitadder_5_carry_out, n1bitadder_5_result, n1bitadder_6_carry_out,
       n1bitadder_6_result, n1bitadder_7_carry_out, n1bitadder_7_result, n1bitadder_8_carry_out,
       n1bitadder_8_result, n1bitadder_9_carry_out, n1bitadder_9_result, n1bitadder_10_carry_out,
       n1bitadder_10_result, n1bitadder_11_carry_out, n1bitadder_11_result, n1bitadder_12_carry_out,
       n1bitadder_12_result, n1bitadder_13_carry_out, n1bitadder_13_result, n1bitadder_14_carry_out,
       n1bitadder_14_result, n1bitadder_15_carry_out, n1bitadder_15_result, n1bitalu_0_1_b_invert_pass,
       n1bitalu_0_1_carry_out, n1bitalu_0_1_result, n1bitalu_1_b_invert_pass, n1bitalu_1_carry_out,
       n1bitalu_1_result, n1bitalu_2_b_invert_pass, n1bitalu_2_carry_out, n1bitalu_2_result,
       n1bitalu_3_b_invert_pass, n1bitalu_3_carry_out, n1bitalu_3_result, n1bitalu_4_b_invert_pass,
       n1bitalu_4_carry_out, n1bitalu_4_result, n1bitalu_5_b_invert_pass, n1bitalu_5_carry_out,
       n1bitalu_5_result, n1bitalu_6_b_invert_pass, n1bitalu_6_carry_out, n1bitalu_6_result,
       n1bitalu_7_b_invert_pass, n1bitalu_7_carry_out, n1bitalu_7_result, n4bitmult_1_output_0,
       n4bitmult_1_output_1, n4bitmult_1_output_2, n4bitmult_1_output_3, n4bitmult_1_output_4,
       n4bitmult_1_output_5, n4bitmult_1_output_6, n4bitmult_1_output_7, n4bitmult_2_output_0,
       n4bitmult_2_output_1, n4bitmult_2_output_2, n4bitmult_2_output_3, n4bitmult_2_output_4,
       n4bitmult_2_output_5, n4bitmult_2_output_6, n4bitmult_2_output_7, n4bitmult_3_output_0,
       n4bitmult_3_output_1, n4bitmult_3_output_2, n4bitmult_3_output_3, n4bitmult_3_output_4,
       n4bitmult_3_output_5, n4bitmult_3_output_6, n4bitmult_3_output_7, n4bitmult_4_output_0,
       n4bitmult_4_output_1, n4bitmult_4_output_2, n4bitmult_4_output_3, n4bitmult_4_output_4,
       n4bitmult_4_output_5, n4bitmult_4_output_6, n4bitmult_4_output_7, not_1_out, not_2_out, not_3_out,
       not_4_out, not_5_out, not_6_out, not_7_out, not_8_out, not_9_out, or_10_out, or_11_out, or_12_out,
       xor_gate_1_output;

  _1bitALU_0 u_1bitalu_0_1 (
    .Input_A(Input_A0), .Input_B(Input_B0), .B_Invert(add_sub), .B_Invert_pass(n1bitalu_0_1_b_invert_pass),
    .Carry_Out(n1bitalu_0_1_carry_out), .Result(n1bitalu_0_1_result));
  _1bitALU u_1bitalu_1 (
    .Input_A(Input_A1), .Input_B(Input_B1), .Result(n1bitalu_1_result),
    .B_Invert(n1bitalu_0_1_b_invert_pass), .Carry_In(n1bitalu_0_1_carry_out),
    .B_Invert_pass(n1bitalu_1_b_invert_pass), .Carry_Out(n1bitalu_1_carry_out));
  _1bitALU u_1bitalu_2 (
    .Input_A(Input_A2), .Input_B(Input_B2), .Result(n1bitalu_2_result), .B_Invert(n1bitalu_1_b_invert_pass),
    .Carry_In(n1bitalu_1_carry_out), .B_Invert_pass(n1bitalu_2_b_invert_pass),
    .Carry_Out(n1bitalu_2_carry_out));
  _1bitALU u_1bitalu_3 (
    .Input_A(Input_A3), .Input_B(Input_B3), .Result(n1bitalu_3_result), .B_Invert(n1bitalu_2_b_invert_pass),
    .Carry_In(n1bitalu_2_carry_out), .B_Invert_pass(n1bitalu_3_b_invert_pass),
    .Carry_Out(n1bitalu_3_carry_out));
  _1bitALU u_1bitalu_4 (
    .Input_A(Input_A4), .Input_B(Input_B4), .Result(n1bitalu_4_result), .B_Invert(n1bitalu_3_b_invert_pass),
    .Carry_In(n1bitalu_3_carry_out), .B_Invert_pass(n1bitalu_4_b_invert_pass),
    .Carry_Out(n1bitalu_4_carry_out));
  _1bitALU u_1bitalu_5 (
    .Input_A(Input_A5), .Input_B(Input_B5), .Result(n1bitalu_5_result), .B_Invert(n1bitalu_4_b_invert_pass),
    .Carry_In(n1bitalu_4_carry_out), .B_Invert_pass(n1bitalu_5_b_invert_pass),
    .Carry_Out(n1bitalu_5_carry_out));
  _1bitALU u_1bitalu_6 (
    .Input_A(Input_A6), .Input_B(Input_B6), .Result(n1bitalu_6_result), .B_Invert(n1bitalu_5_b_invert_pass),
    .Carry_In(n1bitalu_5_carry_out), .B_Invert_pass(n1bitalu_6_b_invert_pass),
    .Carry_Out(n1bitalu_6_carry_out));
  _1bitALU u_1bitalu_7 (
    .Input_A(Input_A7), .Input_B(Input_B7), .Result(n1bitalu_7_result), .B_Invert(n1bitalu_6_b_invert_pass),
    .Carry_In(n1bitalu_6_carry_out), .B_Invert_pass(n1bitalu_7_b_invert_pass),
    .Carry_Out(n1bitalu_7_carry_out));
  XOR_gate xor_gate_1 (.Input_A(n1bitalu_7_carry_out), .Input_B(n1bitalu_7_b_invert_pass), .Output(xor_gate_1_output));
  not not_1 (not_1_out, mult);
  not not_2 (not_2_out, mult);
  not not_3 (not_3_out, mult);
  not not_4 (not_4_out, mult);
  not not_5 (not_5_out, mult);
  not not_6 (not_6_out, mult);
  not not_7 (not_7_out, mult);
  not not_8 (not_8_out, mult);
  not not_9 (not_9_out, mult);
  _4bitMult u_4bitmult_1 (
    .Input_A0(Input_A0), .Input_A1(Input_A1), .Input_A2(Input_A2), .Input_A3(Input_A3), .Input_B0(Input_B0),
    .Input_B1(Input_B1), .Input_B2(Input_B2), .Input_B3(Input_B3), .Output_0(n4bitmult_1_output_0),
    .Output_1(n4bitmult_1_output_1), .Output_2(n4bitmult_1_output_2), .Output_3(n4bitmult_1_output_3),
    .Output_4(n4bitmult_1_output_4), .Output_5(n4bitmult_1_output_5), .Output_6(n4bitmult_1_output_6),
    .Output_7(n4bitmult_1_output_7));
  _4bitMult u_4bitmult_2 (
    .Input_A0(Input_A0), .Input_A1(Input_A1), .Input_A2(Input_A2), .Input_A3(Input_A3), .Input_B0(Input_B4),
    .Input_B1(Input_B5), .Input_B2(Input_B6), .Input_B3(Input_B7), .Output_0(n4bitmult_2_output_0),
    .Output_1(n4bitmult_2_output_1), .Output_2(n4bitmult_2_output_2), .Output_3(n4bitmult_2_output_3),
    .Output_4(n4bitmult_2_output_4), .Output_5(n4bitmult_2_output_5), .Output_6(n4bitmult_2_output_6),
    .Output_7(n4bitmult_2_output_7));
  _4bitMult u_4bitmult_3 (
    .Input_A0(Input_A4), .Input_A1(Input_A5), .Input_A2(Input_A6), .Input_A3(Input_A7), .Input_B0(Input_B0),
    .Input_B1(Input_B1), .Input_B2(Input_B2), .Input_B3(Input_B3), .Output_0(n4bitmult_3_output_0),
    .Output_1(n4bitmult_3_output_1), .Output_2(n4bitmult_3_output_2), .Output_3(n4bitmult_3_output_3),
    .Output_4(n4bitmult_3_output_4), .Output_5(n4bitmult_3_output_5), .Output_6(n4bitmult_3_output_6),
    .Output_7(n4bitmult_3_output_7));
  _4bitMult u_4bitmult_4 (
    .Input_A0(Input_A4), .Input_A1(Input_A5), .Input_A2(Input_A6), .Input_A3(Input_A7), .Input_B0(Input_B4),
    .Input_B1(Input_B5), .Input_B2(Input_B6), .Input_B3(Input_B7), .Output_0(n4bitmult_4_output_0),
    .Output_1(n4bitmult_4_output_1), .Output_2(n4bitmult_4_output_2), .Output_3(n4bitmult_4_output_3),
    .Output_4(n4bitmult_4_output_4), .Output_5(n4bitmult_4_output_5), .Output_6(n4bitmult_4_output_6),
    .Output_7(n4bitmult_4_output_7));
  and and_1 (and_1_out, n1bitalu_0_1_result, not_1_out);
  and and_2 (and_2_out, n1bitalu_1_result, not_2_out);
  and and_3 (and_3_out, n1bitalu_2_result, not_3_out);
  and and_4 (and_4_out, n1bitalu_3_result, not_4_out);
  and and_5 (and_5_out, n1bitalu_4_result, not_5_out);
  and and_6 (and_6_out, n1bitalu_5_result, not_6_out);
  and and_7 (and_7_out, n1bitalu_6_result, not_7_out);
  and and_8 (and_8_out, n1bitalu_7_result, not_8_out);
  and and_9 (and_9_out, xor_gate_1_output, not_9_out);
  and and_10 (and_10_out, n4bitmult_1_output_1, mult);
  and and_11 (and_11_out, n4bitmult_1_output_0, mult);
  and and_12 (and_12_out, n4bitmult_1_output_2, mult);
  and and_13 (and_13_out, n4bitmult_1_output_3, mult);
  and and_14 (and_14_out, n1bitadder_0_2_result, mult);
  and and_15 (and_15_out, n1bitadder_8_result, mult);
  and and_16 (and_16_out, n1bitadder_10_result, mult);
  and and_17 (and_17_out, n1bitadder_9_result, mult);
  or or_1 (Output_0, and_11_out, and_1_out);
  or or_2 (Output_1, and_10_out, and_2_out);
  or or_3 (Output_2, and_12_out, and_3_out);
  or or_4 (Output_3, and_13_out, and_4_out);
  or or_5 (Output_4, and_14_out, and_5_out);
  or or_6 (Output_5, and_15_out, and_6_out);
  or or_7 (Output_6, and_17_out, and_7_out);
  or or_8 (Output_7, and_16_out, and_8_out);
  or or_9 (Overflow, and_18_out, and_9_out);
  and and_18 (and_18_out, or_10_out, mult);
  or or_10 (or_10_out, or_12_out, n1bitadder_15_result, n1bitadder_14_result, n1bitadder_13_result, n1bitadder_12_result, n1bitadder_11_result);
  _1bitAdder_0 u_1bitadder_0_1 (
    .Input_A(n4bitmult_2_output_0), .Input_B(n4bitmult_3_output_0), .Carry_Out(n1bitadder_0_1_carry_out),
    .Result(n1bitadder_0_1_result));
  _1bitAdder u_1bitadder_1 (
    .Input_A(n4bitmult_2_output_1), .Input_B(n4bitmult_3_output_1), .Result(n1bitadder_1_result),
    .Carry_In(n1bitadder_0_1_carry_out), .Carry_Out(n1bitadder_1_carry_out));
  _1bitAdder u_1bitadder_2 (
    .Input_A(n4bitmult_2_output_2), .Input_B(n4bitmult_3_output_2), .Result(n1bitadder_2_result),
    .Carry_In(n1bitadder_1_carry_out), .Carry_Out(n1bitadder_2_carry_out));
  _1bitAdder u_1bitadder_3 (
    .Input_A(n4bitmult_2_output_3), .Input_B(n4bitmult_3_output_3), .Result(n1bitadder_3_result),
    .Carry_In(n1bitadder_2_carry_out), .Carry_Out(n1bitadder_3_carry_out));
  _1bitAdder u_1bitadder_4 (
    .Input_A(n4bitmult_2_output_4), .Input_B(n4bitmult_3_output_4), .Result(n1bitadder_4_result),
    .Carry_In(n1bitadder_3_carry_out), .Carry_Out(n1bitadder_4_carry_out));
  _1bitAdder u_1bitadder_5 (
    .Input_A(n4bitmult_2_output_5), .Input_B(n4bitmult_3_output_5), .Result(n1bitadder_5_result),
    .Carry_In(n1bitadder_4_carry_out), .Carry_Out(n1bitadder_5_carry_out));
  _1bitAdder u_1bitadder_6 (
    .Input_A(n4bitmult_2_output_6), .Input_B(n4bitmult_3_output_6), .Result(n1bitadder_6_result),
    .Carry_In(n1bitadder_5_carry_out), .Carry_Out(n1bitadder_6_carry_out));
  _1bitAdder u_1bitadder_7 (
    .Input_A(n4bitmult_2_output_7), .Input_B(n4bitmult_3_output_7), .Result(n1bitadder_7_result),
    .Carry_In(n1bitadder_6_carry_out), .Carry_Out(n1bitadder_7_carry_out));
  _1bitAdder_0 u_1bitadder_0_2 (
    .Input_A(n4bitmult_1_output_4), .Input_B(n1bitadder_0_1_result), .Carry_Out(n1bitadder_0_2_carry_out),
    .Result(n1bitadder_0_2_result));
  _1bitAdder u_1bitadder_8 (
    .Input_A(n4bitmult_1_output_5), .Input_B(n1bitadder_1_result), .Result(n1bitadder_8_result),
    .Carry_In(n1bitadder_0_2_carry_out), .Carry_Out(n1bitadder_8_carry_out));
  _1bitAdder u_1bitadder_9 (
    .Input_A(n4bitmult_1_output_6), .Input_B(n1bitadder_2_result), .Result(n1bitadder_9_result),
    .Carry_In(n1bitadder_8_carry_out), .Carry_Out(n1bitadder_9_carry_out));
  _1bitAdder u_1bitadder_10 (
    .Input_A(n4bitmult_1_output_7), .Input_B(n1bitadder_3_result), .Result(n1bitadder_10_result),
    .Carry_In(n1bitadder_9_carry_out), .Carry_Out(n1bitadder_10_carry_out));
  _1bitAdder u_1bitadder_11 (
    .Input_A(n4bitmult_4_output_0), .Input_B(n1bitadder_4_result), .Result(n1bitadder_11_result),
    .Carry_In(n1bitadder_10_carry_out), .Carry_Out(n1bitadder_11_carry_out));
  _1bitAdder u_1bitadder_12 (
    .Input_A(n4bitmult_4_output_1), .Input_B(n1bitadder_5_result), .Result(n1bitadder_12_result),
    .Carry_In(n1bitadder_11_carry_out), .Carry_Out(n1bitadder_12_carry_out));
  _1bitAdder u_1bitadder_13 (
    .Input_A(n4bitmult_4_output_2), .Input_B(n1bitadder_6_result), .Result(n1bitadder_13_result),
    .Carry_In(n1bitadder_12_carry_out), .Carry_Out(n1bitadder_13_carry_out));
  _1bitAdder u_1bitadder_14 (
    .Input_A(n4bitmult_4_output_3), .Input_B(n1bitadder_7_result), .Result(n1bitadder_14_result),
    .Carry_In(n1bitadder_13_carry_out), .Carry_Out(n1bitadder_14_carry_out));
  _1bitAdder u_1bitadder_15 (
    .Input_A(n4bitmult_4_output_4), .Input_B(n1bitadder_7_carry_out), .Result(n1bitadder_15_result),
    .Carry_In(n1bitadder_14_carry_out), .Carry_Out(n1bitadder_15_carry_out));
  or or_11 (or_11_out, Output_0, Output_1, Output_2, Output_3, Output_4, Output_5, Output_6, Output_7, Overflow);
  not not_10 (Zero, or_11_out);
  or or_12 (or_12_out, n1bitadder_15_carry_out, n4bitmult_4_output_5, n4bitmult_4_output_6, n4bitmult_4_output_7);
endmodule

module _8bitAdd_Sub (
  input  Add_Sub,
  input  Input_A,
  input  in_3,
  input  in_4,
  input  in_5,
  input  in_6,
  input  in_7,
  input  in_8,
  input  in_9,
  input  Input_B,
  input  in_11,
  input  in_12,
  input  in_13,
  input  in_14,
  input  in_15,
  input  in_16,
  input  in_17,
  output Result,
  output out_19,
  output out_20,
  output out_21,
  output out_22,
  output out_23,
  output out_24,
  output out_25,
  output B_Invert_pass,
  output Carry_Out
);

  wire n1bitalu_0_1_b_invert_pass, n1bitalu_0_1_carry_out, n1bitalu_1_b_invert_pass, n1bitalu_1_carry_out,
       n1bitalu_2_b_invert_pass, n1bitalu_2_carry_out, n1bitalu_3_b_invert_pass, n1bitalu_3_carry_out,
       n1bitalu_4_b_invert_pass, n1bitalu_4_carry_out, n1bitalu_5_b_invert_pass, n1bitalu_5_carry_out,
       n1bitalu_6_b_invert_pass, n1bitalu_6_carry_out;

  _1bitALU_0 u_1bitalu_0_1 (
    .Input_A(Input_A), .Input_B(Input_B), .B_Invert(Add_Sub), .B_Invert_pass(n1bitalu_0_1_b_invert_pass),
    .Carry_Out(n1bitalu_0_1_carry_out), .Result(Result));
  _1bitALU u_1bitalu_1 (
    .Input_A(in_3), .Input_B(in_11), .Result(out_19), .B_Invert(n1bitalu_0_1_b_invert_pass),
    .Carry_In(n1bitalu_0_1_carry_out), .B_Invert_pass(n1bitalu_1_b_invert_pass),
    .Carry_Out(n1bitalu_1_carry_out));
  _1bitALU u_1bitalu_2 (
    .Input_A(in_4), .Input_B(in_12), .Result(out_20), .B_Invert(n1bitalu_1_b_invert_pass),
    .Carry_In(n1bitalu_1_carry_out), .B_Invert_pass(n1bitalu_2_b_invert_pass),
    .Carry_Out(n1bitalu_2_carry_out));
  _1bitALU u_1bitalu_3 (
    .Input_A(in_5), .Input_B(in_13), .Result(out_21), .B_Invert(n1bitalu_2_b_invert_pass),
    .Carry_In(n1bitalu_2_carry_out), .B_Invert_pass(n1bitalu_3_b_invert_pass),
    .Carry_Out(n1bitalu_3_carry_out));
  _1bitALU u_1bitalu_4 (
    .Input_A(in_6), .Input_B(in_14), .Result(out_22), .B_Invert(n1bitalu_3_b_invert_pass),
    .Carry_In(n1bitalu_3_carry_out), .B_Invert_pass(n1bitalu_4_b_invert_pass),
    .Carry_Out(n1bitalu_4_carry_out));
  _1bitALU u_1bitalu_5 (
    .Input_A(in_7), .Input_B(in_15), .Result(out_23), .B_Invert(n1bitalu_4_b_invert_pass),
    .Carry_In(n1bitalu_4_carry_out), .B_Invert_pass(n1bitalu_5_b_invert_pass),
    .Carry_Out(n1bitalu_5_carry_out));
  _1bitALU u_1bitalu_6 (
    .Input_A(in_8), .Input_B(in_16), .Result(out_24), .B_Invert(n1bitalu_5_b_invert_pass),
    .Carry_In(n1bitalu_5_carry_out), .B_Invert_pass(n1bitalu_6_b_invert_pass),
    .Carry_Out(n1bitalu_6_carry_out));
  _1bitALU u_1bitalu_7 (
    .Input_A(in_9), .Input_B(in_17), .Result(out_25), .B_Invert(n1bitalu_6_b_invert_pass),
    .Carry_In(n1bitalu_6_carry_out), .B_Invert_pass(B_Invert_pass), .Carry_Out(Carry_Out));
endmodule

module _1bitALU_0 (
  input  B_Invert,
  input  Input_A,
  input  Input_B,
  output Result,
  output B_Invert_pass,
  output Carry_Out
);

  wire and_1_out, and_2_out, and_3_out, and_4_out, and_5_out, not_1_out, not_2_out, not_3_out, not_4_out,
       or_1_out, or_2_out, or_3_out;

  not not_1 (not_1_out, Input_B);
  not not_2 (not_2_out, B_Invert);
  and and_1 (and_1_out, B_Invert, not_1_out);
  and and_2 (and_2_out, Input_B, not_2_out);
  or or_1 (or_1_out, and_1_out, and_2_out);
  or or_2 (or_2_out, Input_A, or_1_out);
  and and_3 (and_3_out, Input_A, or_1_out);
  not not_3 (not_3_out, and_3_out);
  and and_4 (and_4_out, or_2_out, not_3_out);
  or or_3 (or_3_out, B_Invert, and_4_out);
  and and_5 (and_5_out, B_Invert, and_4_out);
  not not_4 (not_4_out, and_5_out);
  and and_6 (Result, or_3_out, not_4_out);
  or or_4 (Carry_Out, and_5_out, and_3_out);

  assign B_Invert_pass = B_Invert;
endmodule

module _1bitALU (
  input  B_Invert,
  input  Carry_In,
  input  Input_A,
  input  Input_B,
  output Result,
  output B_Invert_pass,
  output Carry_Out
);

  wire and_1_out, and_2_out, and_3_out, and_4_out, and_5_out, not_1_out, not_2_out, not_3_out, not_4_out,
       or_1_out, or_2_out, or_3_out;

  not not_1 (not_1_out, Input_B);
  not not_2 (not_2_out, B_Invert);
  and and_1 (and_1_out, B_Invert, not_1_out);
  and and_2 (and_2_out, Input_B, not_2_out);
  or or_1 (or_1_out, and_1_out, and_2_out);
  or or_2 (or_2_out, Input_A, or_1_out);
  and and_3 (and_3_out, Input_A, or_1_out);
  not not_3 (not_3_out, and_3_out);
  and and_4 (and_4_out, or_2_out, not_3_out);
  or or_3 (or_3_out, Carry_In, and_4_out);
  and and_5 (and_5_out, Carry_In, and_4_out);
  not not_4 (not_4_out, and_5_out);
  and and_6 (Result, or_3_out, not_4_out);
  or or_4 (Carry_Out, and_5_out, and_3_out);

  assign B_Invert_pass = B_Invert;
endmodule

// 2 bit Mult
module _2bitMult (
  input  Input_A0,
  input  Input_A1,
  input  Input_B0,
  input  Input_B1,
  output Output_0,
  output Output_1,
  output Output_2,
  output Output_3
);

  wire and_1_out, and_3_out, and_4_out, and_5_out;

  and and_1 (and_1_out, Input_A0, Input_B1);
  and and_2 (Output_0, Input_A0, Input_B0);
  and and_3 (and_3_out, Input_A1, Input_B0);
  and and_4 (and_4_out, Input_A1, Input_B1);
  XOR_gate xor_gate_1 (.Input_A(and_1_out), .Input_B(and_3_out), .Output(Output_1));
  and and_5 (and_5_out, and_1_out, and_3_out);
  XOR_gate xor_gate_2 (.Input_A(and_5_out), .Input_B(and_4_out), .Output(Output_2));
  and and_6 (Output_3, and_5_out, and_4_out);
endmodule

// 4 bit Mult
module _4bitMult (
  input  Input_A0,
  input  Input_A1,
  input  Input_A2,
  input  Input_A3,
  input  Input_B0,
  input  Input_B1,
  input  Input_B2,
  input  Input_B3,
  output Output_0,
  output Output_1,
  output Output_2,
  output Output_3,
  output Output_4,
  output Output_5,
  output Output_6,
  output Output_7
);

  wire n1bitadder_0_1_carry_out, n1bitadder_0_1_result, n1bitadder_0_2_carry_out, n1bitadder_1_carry_out,
       n1bitadder_1_result, n1bitadder_2_carry_out, n1bitadder_2_result, n1bitadder_3_carry_out,
       n1bitadder_3_result, n1bitadder_4_carry_out, n1bitadder_5_carry_out, n1bitadder_6_carry_out,
       n1bitadder_7_carry_out, n2bitmult_1_output_2, n2bitmult_1_output_3, n2bitmult_2_output_0,
       n2bitmult_2_output_1, n2bitmult_2_output_2, n2bitmult_2_output_3, n2bitmult_3_output_0,
       n2bitmult_3_output_1, n2bitmult_3_output_2, n2bitmult_3_output_3, n2bitmult_4_output_0,
       n2bitmult_4_output_1, n2bitmult_4_output_2, n2bitmult_4_output_3;

  _2bitMult u_2bitmult_1 (
    .Input_A0(Input_A0), .Input_A1(Input_A1), .Input_B0(Input_B0), .Input_B1(Input_B1), .Output_0(Output_0),
    .Output_1(Output_1), .Output_2(n2bitmult_1_output_2), .Output_3(n2bitmult_1_output_3));
  _2bitMult u_2bitmult_2 (
    .Input_A0(Input_A0), .Input_A1(Input_A1), .Input_B0(Input_B2), .Input_B1(Input_B3),
    .Output_0(n2bitmult_2_output_0), .Output_1(n2bitmult_2_output_1), .Output_2(n2bitmult_2_output_2),
    .Output_3(n2bitmult_2_output_3));
  _2bitMult u_2bitmult_3 (
    .Input_A0(Input_A2), .Input_A1(Input_A3), .Input_B0(Input_B0), .Input_B1(Input_B1),
    .Output_0(n2bitmult_3_output_0), .Output_1(n2bitmult_3_output_1), .Output_2(n2bitmult_3_output_2),
    .Output_3(n2bitmult_3_output_3));
  _2bitMult u_2bitmult_4 (
    .Input_A0(Input_A2), .Input_A1(Input_A3), .Input_B0(Input_B2), .Input_B1(Input_B3),
    .Output_0(n2bitmult_4_output_0), .Output_1(n2bitmult_4_output_1), .Output_2(n2bitmult_4_output_2),
    .Output_3(n2bitmult_4_output_3));
  _1bitAdder_0 u_1bitadder_0_1 (
    .Input_A(n2bitmult_2_output_0), .Input_B(n2bitmult_3_output_0), .Carry_Out(n1bitadder_0_1_carry_out),
    .Result(n1bitadder_0_1_result));
  _1bitAdder u_1bitadder_1 (
    .Input_A(n2bitmult_2_output_1), .Input_B(n2bitmult_3_output_1), .Result(n1bitadder_1_result),
    .Carry_In(n1bitadder_0_1_carry_out), .Carry_Out(n1bitadder_1_carry_out));
  _1bitAdder u_1bitadder_2 (
    .Input_A(n2bitmult_2_output_2), .Input_B(n2bitmult_3_output_2), .Result(n1bitadder_2_result),
    .Carry_In(n1bitadder_1_carry_out), .Carry_Out(n1bitadder_2_carry_out));
  _1bitAdder u_1bitadder_3 (
    .Input_A(n2bitmult_2_output_3), .Input_B(n2bitmult_3_output_3), .Result(n1bitadder_3_result),
    .Carry_In(n1bitadder_2_carry_out), .Carry_Out(n1bitadder_3_carry_out));
  _1bitAdder_0 u_1bitadder_0_2 (
    .Input_A(n2bitmult_1_output_2), .Input_B(n1bitadder_0_1_result), .Carry_Out(n1bitadder_0_2_carry_out),
    .Result(Output_2));
  _1bitAdder u_1bitadder_4 (
    .Input_A(n2bitmult_1_output_3), .Input_B(n1bitadder_1_result), .Result(Output_3),
    .Carry_In(n1bitadder_0_2_carry_out), .Carry_Out(n1bitadder_4_carry_out));
  _1bitAdder u_1bitadder_5 (
    .Input_A(n1bitadder_2_result), .Input_B(n2bitmult_4_output_0), .Result(Output_4),
    .Carry_In(n1bitadder_4_carry_out), .Carry_Out(n1bitadder_5_carry_out));
  _1bitAdder u_1bitadder_6 (
    .Input_A(n1bitadder_3_result), .Input_B(n2bitmult_4_output_1), .Result(Output_5),
    .Carry_In(n1bitadder_5_carry_out), .Carry_Out(n1bitadder_6_carry_out));
  _1bitAdder u_1bitadder_7 (
    .Input_A(n1bitadder_3_carry_out), .Input_B(n2bitmult_4_output_2), .Result(Output_6),
    .Carry_In(n1bitadder_6_carry_out), .Carry_Out(n1bitadder_7_carry_out));
  _1bitAdder_0 u_1bitadder_0_3 (
    .Input_A(n1bitadder_7_carry_out), .Input_B(n2bitmult_4_output_3), .Result(Output_7));  // open: Carry_Out
endmodule

module _1bitAdder_0 (
  input  Input_A,
  input  Input_B,
  output Result,
  output Carry_Out
);

  wire not_1_out, or_1_out;

  or or_1 (or_1_out, Input_A, Input_B);
  and and_1 (Carry_Out, Input_A, Input_B);
  not not_1 (not_1_out, Carry_Out);
  and and_2 (Result, or_1_out, not_1_out);
endmodule

module _1bitAdder (
  input  Carry_In,
  input  Input_A,
  input  Input_B,
  output Result,
  output Carry_Out
);

  wire and_1_out, and_2_out, and_3_out, not_1_out, not_2_out, or_1_out, or_2_out;

  or or_1 (or_1_out, Input_A, Input_B);
  and and_1 (and_1_out, Input_A, Input_B);
  not not_1 (not_1_out, and_1_out);
  and and_2 (and_2_out, or_1_out, not_1_out);
  or or_2 (or_2_out, Carry_In, and_2_out);
  and and_3 (and_3_out, Carry_In, and_2_out);
  not not_2 (not_2_out, and_3_out);
  and and_4 (Result, or_2_out, not_2_out);
  or or_3 (Carry_Out, and_3_out, and_1_out);
endmodule

// XOR
module XOR_gate (
  input  Input_A,
  input  Input_B,
  output Output
);

  wire and_1_out, not_1_out, or_1_out;

  and and_1 (and_1_out, Input_A, Input_B);
  or or_1 (or_1_out, Input_A, Input_B);
  not not_1 (not_1_out, and_1_out);
  and and_2 (Output, not_1_out, or_1_out);
endmodule

module Keypad (
  input  in_1,
  input  in_2,
  input  in_3,
  input  in_4,
  input  in_5,
  input  in_6,
  input  in_7,
  input  in_8,
  input  in_9,
  input  in_10,
  input  in_11,
  output out_12,
  output out_13,
  output out_14,
  output out_15,
  output out_16,
  output out_17,
  output out_18,
  output out_19
);

  wire [7:0] and_1_out, and_2_out, and_3_out, and_4_out, and_5_out, and_6_out, and_7_out, and_8_out,
       and_9_out, and_10_out, n8bitadd_sub_1_result, n8bitadd_sub_2_result, n8bitadd_sub_3_result,
       n8bitadd_sub_4_result, n8bitadd_sub_5_result, n8bitadd_sub_6_result, n8bitadd_sub_7_result,
       n8bitadd_sub_8_result, n8bitadd_sub_9_result;

  assign and_1_out = {8{in_1}} & 8'h1;  // AND_Gate and_1, 8 bits wide
  _8bitAdd_Sub u_8bitadd_sub_1 (
    .Input_A(and_2_out[0]), .in_3(and_2_out[1]), .in_4(and_2_out[2]), .in_5(and_2_out[3]),
    .in_6(and_2_out[4]), .in_7(and_2_out[5]), .in_8(and_2_out[6]), .in_9(and_2_out[7]),
    .Input_B(and_1_out[0]), .in_11(and_1_out[1]), .in_12(and_1_out[2]), .in_13(and_1_out[3]),
    .in_14(and_1_out[4]), .in_15(and_1_out[5]), .in_16(and_1_out[6]), .in_17(and_1_out[7]), .Add_Sub(1'b0),
    .Result(n8bitadd_sub_1_result[0]), .out_19(n8bitadd_sub_1_result[1]), .out_20(n8bitadd_sub_1_result[2]),
    .out_21(n8bitadd_sub_1_result[3]), .out_22(n8bitadd_sub_1_result[4]), .out_23(n8bitadd_sub_1_result[5]),
    .out_24(n8bitadd_sub_1_result[6]), .out_25(n8bitadd_sub_1_result[7]));  // open: B_Invert_pass, Carry_Out
  assign and_2_out = {8{in_2}} & 8'h2;  // AND_Gate and_2, 8 bits wide
  _8bitAdd_Sub u_8bitadd_sub_2 (
    .Input_A(n8bitadd_sub_5_result[0]), .in_3(n8bitadd_sub_5_result[1]), .in_4(n8bitadd_sub_5_result[2]),
    .in_5(n8bitadd_sub_5_result[3]), .in_6(n8bitadd_sub_5_result[4]), .in_7(n8bitadd_sub_5_result[5]),
    .in_8(n8bitadd_sub_5_result[6]), .in_9(n8bitadd_sub_5_result[7]), .Input_B(n8bitadd_sub_1_result[0]),
    .in_11(n8bitadd_sub_1_result[1]), .in_12(n8bitadd_sub_1_result[2]), .in_13(n8bitadd_sub_1_result[3]),
    .in_14(n8bitadd_sub_1_result[4]), .in_15(n8bitadd_sub_1_result[5]), .in_16(n8bitadd_sub_1_result[6]),
    .in_17(n8bitadd_sub_1_result[7]), .Add_Sub(1'b0), .Result(n8bitadd_sub_2_result[0]),
    .out_19(n8bitadd_sub_2_result[1]), .out_20(n8bitadd_sub_2_result[2]), .out_21(n8bitadd_sub_2_result[3]),
    .out_22(n8bitadd_sub_2_result[4]), .out_23(n8bitadd_sub_2_result[5]), .out_24(n8bitadd_sub_2_result[6]),
    .out_25(n8bitadd_sub_2_result[7]));  // open: B_Invert_pass, Carry_Out
  assign and_3_out = {8{in_4}} & 8'h4;  // AND_Gate and_3, 8 bits wide
  assign and_4_out = {8{in_3}} & 8'h3;  // AND_Gate and_4, 8 bits wide
  _8bitAdd_Sub u_8bitadd_sub_3 (
    .Input_A(and_3_out[0]), .in_3(and_3_out[1]), .in_4(and_3_out[2]), .in_5(and_3_out[3]),
    .in_6(and_3_out[4]), .in_7(and_3_out[5]), .in_8(and_3_out[6]), .in_9(and_3_out[7]),
    .Input_B(and_4_out[0]), .in_11(and_4_out[1]), .in_12(and_4_out[2]), .in_13(and_4_out[3]),
    .in_14(and_4_out[4]), .in_15(and_4_out[5]), .in_16(and_4_out[6]), .in_17(and_4_out[7]), .Add_Sub(1'b0),
    .Result(n8bitadd_sub_3_result[0]), .out_19(n8bitadd_sub_3_result[1]), .out_20(n8bitadd_sub_3_result[2]),
    .out_21(n8bitadd_sub_3_result[3]), .out_22(n8bitadd_sub_3_result[4]), .out_23(n8bitadd_sub_3_result[5]),
    .out_24(n8bitadd_sub_3_result[6]), .out_25(n8bitadd_sub_3_result[7]));  // open: B_Invert_pass, Carry_Out
  D_Flip_Flop d_ff_1 (.clk(in_11), .D(n8bitadd_sub_6_result[7]), .Q(out_12));  // open: Qn, preset, en, reset
  assign and_5_out = {8{in_5}} & 8'h5;  // AND_Gate and_5, 8 bits wide
  D_Flip_Flop d_ff_2 (.clk(in_11), .D(n8bitadd_sub_6_result[6]), .Q(out_13));  // open: Qn, preset, en, reset
  assign and_6_out = {8{in_6}} & 8'h6;  // AND_Gate and_6, 8 bits wide
  _8bitAdd_Sub u_8bitadd_sub_4 (
    .Input_A(and_6_out[0]), .in_3(and_6_out[1]), .in_4(and_6_out[2]), .in_5(and_6_out[3]),
    .in_6(and_6_out[4]), .in_7(and_6_out[5]), .in_8(and_6_out[6]), .in_9(and_6_out[7]),
    .Input_B(and_5_out[0]), .in_11(and_5_out[1]), .in_12(and_5_out[2]), .in_13(and_5_out[3]),
    .in_14(and_5_out[4]), .in_15(and_5_out[5]), .in_16(and_5_out[6]), .in_17(and_5_out[7]), .Add_Sub(1'b0),
    .Result(n8bitadd_sub_4_result[0]), .out_19(n8bitadd_sub_4_result[1]), .out_20(n8bitadd_sub_4_result[2]),
    .out_21(n8bitadd_sub_4_result[3]), .out_22(n8bitadd_sub_4_result[4]), .out_23(n8bitadd_sub_4_result[5]),
    .out_24(n8bitadd_sub_4_result[6]), .out_25(n8bitadd_sub_4_result[7]));  // open: B_Invert_pass, Carry_Out
  _8bitAdd_Sub u_8bitadd_sub_5 (
    .Input_A(n8bitadd_sub_4_result[0]), .in_3(n8bitadd_sub_4_result[1]), .in_4(n8bitadd_sub_4_result[2]),
    .in_5(n8bitadd_sub_4_result[3]), .in_6(n8bitadd_sub_4_result[4]), .in_7(n8bitadd_sub_4_result[5]),
    .in_8(n8bitadd_sub_4_result[6]), .in_9(n8bitadd_sub_4_result[7]), .Input_B(n8bitadd_sub_3_result[0]),
    .in_11(n8bitadd_sub_3_result[1]), .in_12(n8bitadd_sub_3_result[2]), .in_13(n8bitadd_sub_3_result[3]),
    .in_14(n8bitadd_sub_3_result[4]), .in_15(n8bitadd_sub_3_result[5]), .in_16(n8bitadd_sub_3_result[6]),
    .in_17(n8bitadd_sub_3_result[7]), .Add_Sub(1'b0), .Result(n8bitadd_sub_5_result[0]),
    .out_19(n8bitadd_sub_5_result[1]), .out_20(n8bitadd_sub_5_result[2]), .out_21(n8bitadd_sub_5_result[3]),
    .out_22(n8bitadd_sub_5_result[4]), .out_23(n8bitadd_sub_5_result[5]), .out_24(n8bitadd_sub_5_result[6]),
    .out_25(n8bitadd_sub_5_result[7]));  // open: B_Invert_pass, Carry_Out
  D_Flip_Flop d_ff_3 (.clk(in_11), .D(n8bitadd_sub_6_result[5]), .Q(out_14));  // open: Qn, preset, en, reset
  assign and_7_out = {8{in_7}} & 8'h7;  // AND_Gate and_7, 8 bits wide
  _8bitAdd_Sub u_8bitadd_sub_6 (
    .Input_A(n8bitadd_sub_8_result[0]), .in_3(n8bitadd_sub_8_result[1]), .in_4(n8bitadd_sub_8_result[2]),
    .in_5(n8bitadd_sub_8_result[3]), .in_6(n8bitadd_sub_8_result[4]), .in_7(n8bitadd_sub_8_result[5]),
    .in_8(n8bitadd_sub_8_result[6]), .in_9(n8bitadd_sub_8_result[7]), .Input_B(n8bitadd_sub_2_result[0]),
    .in_11(n8bitadd_sub_2_result[1]), .in_12(n8bitadd_sub_2_result[2]), .in_13(n8bitadd_sub_2_result[3]),
    .in_14(n8bitadd_sub_2_result[4]), .in_15(n8bitadd_sub_2_result[5]), .in_16(n8bitadd_sub_2_result[6]),
    .in_17(n8bitadd_sub_2_result[7]), .Add_Sub(1'b0), .Result(n8bitadd_sub_6_result[0]),
    .out_19(n8bitadd_sub_6_result[1]), .out_20(n8bitadd_sub_6_result[2]), .out_21(n8bitadd_sub_6_result[3]),
    .out_22(n8bitadd_sub_6_result[4]), .out_23(n8bitadd_sub_6_result[5]), .out_24(n8bitadd_sub_6_result[6]),
    .out_25(n8bitadd_sub_6_result[7]));  // open: B_Invert_pass, Carry_Out
  D_Flip_Flop d_ff_4 (.clk(in_11), .D(n8bitadd_sub_6_result[4]), .Q(out_15));  // open: Qn, preset, en, reset
  assign and_8_out = {8{in_8}} & 8'h8;  // AND_Gate and_8, 8 bits wide
  _8bitAdd_Sub u_8bitadd_sub_7 (
    .Input_A(and_8_out[0]), .in_3(and_8_out[1]), .in_4(and_8_out[2]), .in_5(and_8_out[3]),
    .in_6(and_8_out[4]), .in_7(and_8_out[5]), .in_8(and_8_out[6]), .in_9(and_8_out[7]),
    .Input_B(and_7_out[0]), .in_11(and_7_out[1]), .in_12(and_7_out[2]), .in_13(and_7_out[3]),
    .in_14(and_7_out[4]), .in_15(and_7_out[5]), .in_16(and_7_out[6]), .in_17(and_7_out[7]), .Add_Sub(1'b0),
    .Result(n8bitadd_sub_7_result[0]), .out_19(n8bitadd_sub_7_result[1]), .out_20(n8bitadd_sub_7_result[2]),
    .out_21(n8bitadd_sub_7_result[3]), .out_22(n8bitadd_sub_7_result[4]), .out_23(n8bitadd_sub_7_result[5]),
    .out_24(n8bitadd_sub_7_result[6]), .out_25(n8bitadd_sub_7_result[7]));  // open: B_Invert_pass, Carry_Out
  D_Flip_Flop d_ff_5 (.clk(in_11), .D(n8bitadd_sub_6_result[3]), .Q(out_16));  // open: Qn, preset, en, reset
  assign and_9_out = {8{in_9}} & 8'h9;  // AND_Gate and_9, 8 bits wide
  _8bitAdd_Sub u_8bitadd_sub_8 (
    .Input_A(n8bitadd_sub_9_result[0]), .in_3(n8bitadd_sub_9_result[1]), .in_4(n8bitadd_sub_9_result[2]),
    .in_5(n8bitadd_sub_9_result[3]), .in_6(n8bitadd_sub_9_result[4]), .in_7(n8bitadd_sub_9_result[5]),
    .in_8(n8bitadd_sub_9_result[6]), .in_9(n8bitadd_sub_9_result[7]), .Input_B(n8bitadd_sub_7_result[0]),
    .in_11(n8bitadd_sub_7_result[1]), .in_12(n8bitadd_sub_7_result[2]), .in_13(n8bitadd_sub_7_result[3]),
    .in_14(n8bitadd_sub_7_result[4]), .in_15(n8bitadd_sub_7_result[5]), .in_16(n8bitadd_sub_7_result[6]),
    .in_17(n8bitadd_sub_7_result[7]), .Add_Sub(1'b0), .Result(n8bitadd_sub_8_result[0]),
    .out_19(n8bitadd_sub_8_result[1]), .out_20(n8bitadd_sub_8_result[2]), .out_21(n8bitadd_sub_8_result[3]),
    .out_22(n8bitadd_sub_8_result[4]), .out_23(n8bitadd_sub_8_result[5]), .out_24(n8bitadd_sub_8_result[6]),
    .out_25(n8bitadd_sub_8_result[7]));  // open: B_Invert_pass, Carry_Out
  D_Flip_Flop d_ff_6 (.clk(in_11), .D(n8bitadd_sub_6_result[2]), .Q(out_17));  // open: Qn, preset, en, reset
  assign and_10_out = {8{in_10}} & {8{1'b0}};  // AND_Gate and_10, 8 bits wide
  _8bitAdd_Sub u_8bitadd_sub_9 (
    .Input_A(and_10_out[0]), .in_3(and_10_out[1]), .in_4(and_10_out[2]), .in_5(and_10_out[3]),
    .in_6(and_10_out[4]), .in_7(and_10_out[5]), .in_8(and_10_out[6]), .in_9(and_10_out[7]),
    .Input_B(and_9_out[0]), .in_11(and_9_out[1]), .in_12(and_9_out[2]), .in_13(and_9_out[3]),
    .in_14(and_9_out[4]), .in_15(and_9_out[5]), .in_16(and_9_out[6]), .in_17(and_9_out[7]), .Add_Sub(1'b0),
    .Result(n8bitadd_sub_9_result[0]), .out_19(n8bitadd_sub_9_result[1]), .out_20(n8bitadd_sub_9_result[2]),
    .out_21(n8bitadd_sub_9_result[3]), .out_22(n8bitadd_sub_9_result[4]), .out_23(n8bitadd_sub_9_result[5]),
    .out_24(n8bitadd_sub_9_result[6]), .out_25(n8bitadd_sub_9_result[7]));  // open: B_Invert_pass, Carry_Out
  D_Flip_Flop d_ff_7 (.clk(in_11), .D(n8bitadd_sub_6_result[1]), .Q(out_18));  // open: Qn, preset, en, reset
  D_Flip_Flop d_ff_8 (.clk(in_11), .D(n8bitadd_sub_6_result[0]), .Q(out_19));  // open: Qn, preset, en, reset
endmodule
