// Logisim project ALUControlblock.circ as structural Verilog: 1 circuit, main circuit main
module main (
  input  ALUOp1,
  input  ALUOp0,
  input  Fn2,
  input  Fn1,
  input  Fn0,
  output Add_Sub,
  output Mult
);

  wire and_1_out, and_2_out, and_3_out, and_4_out, and_5_out, not_1_out, not_2_out, not_3_out, not_4_out,
       not_5_out, not_6_out;

  not not_1 (not_1_out, ALUOp0);
  not not_2 (not_2_out, ALUOp0);
  not not_3 (not_3_out, ALUOp1);
  not not_4 (not_4_out, Fn2);
  not not_5 (not_5_out, Fn2);
  not not_6 (not_6_out, Fn1);
  and and_1 (and_1_out, not_1_out, ALUOp1);
  and and_2 (and_2_out, not_2_out, not_3_out);
  and and_3 (and_3_out, not_4_out, Fn1);
  and and_4 (and_4_out, not_5_out, not_6_out, Fn0);
  and and_5 (and_5_out, and_1_out, and_3_out);
  and and_6 (Mult, and_1_out, and_4_out);
  or or_1 (Add_Sub, and_5_out, and_2_out);

  // Notes on the sheet:
  //   INPUTS
  //   INPUTS
  //   Read Fn
  //   Address
  //   Add(Sub)
  //   Mult
  //   OUTPUTS
endmodule
