// Logisim project CU.circ as structural Verilog: 1 circuit, main circuit main
module main (
  input  in_1,
  input  Op_1,
  input  Op_2,
  input  Fn_1,
  input  Fn_2,
  input  Fn_3,
  input  Fn_4,
  input  IN_1_2,
  input  IN_2,
  input  [2:0] in_10,
  output out_11,
  output ALU_SRC,
  output MemToReg,
  output RegWri,
  output MemRead,
  output out_16,
  output Branch,
  output ALU_OP_1,
  output ALU_OP_2,
  output Read_Keypad,
  output Print,
  output Finished_Cycle
);

  wire _1_out, _2_out, and_1_out, and_2_out, and_3_out, and_4_out, and_6_out, and_7_out, and_8_out,
       and_9_out, and_10_out, and_11_out, and_12_out, j_k_ff_1_q, j_k_ff_2_q, j_k_ff_3_q, j_k_ff_4_q,
       j_k_ff_5_q, j_k_ff_6_q, j_k_ff_7_q, not_1_out, not_2_out, not_3_out, not_4_out, not_5_out, not_6_out,
       not_7_out, not_8_out, not_9_out, not_10_out, not_11_out, not_12_out, not_13_out, not_14_out,
       not_15_out, not_16_out, not_17_out, not_18_out, not_19_out, not_20_out, not_21_out, not_22_out,
       not_23_out, not_24_out, not_25_out, not_26_out, or_1_out, or_3_out, or_5_out, or_8_out;
  wire [2:0] adder_1_out, j_k_ff_8_q;

  not not_1 (not_1_out, Op_1);
  not not_2 (not_2_out, Op_2);
  not not_3 (not_3_out, Fn_2);
  not not_4 (not_4_out, Fn_3);
  J_K_Flip_Flop j_k_ff_1 (.J(IN_1_2), .clk(in_1), .K(not_5_out), .Q(j_k_ff_1_q));  // open: Qn, preset, en, reset
  not not_5 (not_5_out, IN_1_2);
  J_K_Flip_Flop j_k_ff_2 (.J(IN_2), .clk(in_1), .K(not_6_out), .Q(j_k_ff_2_q));  // open: Qn, preset, en, reset
  not not_6 (not_6_out, IN_2);
  buf and_1 (and_1_out, in_1);  // AND_Gate
  Adder #(.width(3)) adder_1 (.a(j_k_ff_8_q), .b(in_10), .out(adder_1_out));  // open: cin, cout
  J_K_Flip_Flop j_k_ff_3 (.J(Op_1), .clk(in_1), .K(not_1_out), .Q(j_k_ff_3_q));  // open: Qn, preset, en, reset
  J_K_Flip_Flop j_k_ff_4 (.J(Op_2), .clk(in_1), .K(not_2_out), .Q(j_k_ff_4_q));  // open: Qn, preset, en, reset
  J_K_Flip_Flop j_k_ff_5 (.J(Fn_2), .clk(in_1), .K(not_3_out), .Q(j_k_ff_5_q));  // open: Qn, preset, en, reset
  J_K_Flip_Flop j_k_ff_6 (.J(Fn_3), .clk(in_1), .K(not_4_out), .Q(j_k_ff_6_q));  // open: Qn, preset, en, reset
  J_K_Flip_Flop j_k_ff_7 (.J(Fn_4), .clk(in_1), .K(not_7_out), .Q(j_k_ff_7_q));  // open: Qn, preset, en, reset
  not not_7 (not_7_out, Fn_4);
  not not_8 (not_8_out, adder_1_out[0]);
  or or_1 (or_1_out, j_k_ff_2_q, j_k_ff_1_q, j_k_ff_3_q, j_k_ff_4_q, j_k_ff_5_q, j_k_ff_6_q, j_k_ff_7_q);
  J_K_Flip_Flop j_k_ff_8 (
    .J(adder_1_out[0]), .clk(and_1_out), .K(not_8_out), .Q(j_k_ff_8_q[0]));  // open: Qn, preset, en, reset
  not not_9 (not_9_out, adder_1_out[1]);
  J_K_Flip_Flop j_k_ff_9 (
    .J(adder_1_out[1]), .clk(and_1_out), .K(not_9_out), .Q(j_k_ff_8_q[1]));  // open: Qn, preset, en, reset
  not not_10 (not_10_out, j_k_ff_6_q);
  not not_11 (not_11_out, j_k_ff_7_q);
  not not_12 (not_12_out, j_k_ff_6_q);
  not not_13 (not_13_out, j_k_ff_3_q);
  not not_14 (not_14_out, j_k_ff_3_q);
  not not_15 (not_15_out, adder_1_out[2]);
  not not_16 (not_16_out, j_k_ff_3_q);
  not not_17 (not_17_out, j_k_ff_4_q);
  not not_18 (not_18_out, j_k_ff_5_q);
  not not_19 (not_19_out, j_k_ff_6_q);
  not not_20 (not_20_out, j_k_ff_7_q);
  not not_21 (not_21_out, j_k_ff_1_q);
  not not_22 (not_22_out, j_k_ff_4_q);
  J_K_Flip_Flop j_k_ff_10 (
    .J(adder_1_out[2]), .clk(and_1_out), .K(not_15_out), .Q(j_k_ff_8_q[2]));  // open: Qn, preset, en, reset
  and and_2 (and_2_out, not_16_out, not_17_out, not_18_out, not_19_out, not_20_out);
  and and_3 (and_3_out, not_16_out, not_17_out, j_k_ff_6_q, not_18_out, not_20_out);
  and and_4 (and_4_out, not_16_out, not_17_out, not_18_out, not_19_out, j_k_ff_7_q);
  and and_5 (Print, not_16_out, not_17_out, j_k_ff_5_q, not_10_out, not_11_out);
  and and_6 (and_6_out, not_16_out, not_17_out, j_k_ff_5_q, not_12_out, j_k_ff_7_q);
  and and_7 (and_7_out, not_16_out, not_17_out, j_k_ff_5_q, j_k_ff_6_q, j_k_ff_7_q);
  and and_8 (and_8_out, j_k_ff_4_q, not_21_out, not_13_out);
  and and_9 (and_9_out, j_k_ff_4_q, j_k_ff_1_q, not_14_out);
  and and_10 (and_10_out, j_k_ff_3_q, not_22_out);
  and and_11 (and_11_out, j_k_ff_3_q, j_k_ff_4_q);
  and _1 (_1_out, j_k_ff_8_q[0], not_24_out, not_23_out);
  not not_23 (not_23_out, j_k_ff_8_q[2]);
  not not_24 (not_24_out, j_k_ff_8_q[1]);
  not not_25 (not_25_out, j_k_ff_8_q[0]);
  and _2 (_2_out, not_25_out, j_k_ff_8_q[1], not_26_out);
  not not_26 (not_26_out, j_k_ff_8_q[2]);
  and and_12 (and_12_out, j_k_ff_5_q, j_k_ff_6_q, j_k_ff_7_q);
  buf or_2 (MemToReg, and_10_out);  // OR_Gate
  or or_3 (or_3_out, and_2_out, and_3_out, and_10_out, and_6_out, and_4_out);
  buf or_4 (MemRead, and_10_out);  // OR_Gate
  buf or_5 (or_5_out, and_11_out);  // OR_Gate
  or or_6 (Branch, and_8_out, and_9_out);
  and and_13 (Finished_Cycle, j_k_ff_8_q[0], j_k_ff_8_q[1], j_k_ff_8_q[2]);
  not not_27 (out_11, and_12_out);
  or or_7 (ALU_SRC, and_11_out, and_10_out);
  and and_14 (RegWri, or_3_out, _2_out);
  or or_8 (or_8_out, and_2_out, and_3_out, Print, and_6_out, and_4_out);
  or or_9 (ALU_OP_2, and_8_out, and_9_out, and_6_out, Print);
  buf or_10 (Read_Keypad, and_6_out);  // OR_Gate
  and and_15 (out_16, or_5_out, _2_out);
  buf and_16 (ALU_OP_1, or_8_out);  // AND_Gate

  // Notes on the sheet:
  //   ADD
  //   SUB
  //   MULT
  //   PRT
  //   INT
  //   RET
  //   BZ
  //   BEQ
  //   LD
  //   STR
  //   ON/OFF
  //   MemWrite
endmodule
