// Logisim project IR.circ as structural Verilog: 1 circuit, main circuit main
module main (
  input  INPUT,
  input  Op2,
  input  Op1,
  input  Op0,
  input  Addr4,
  input  Addr3,
  input  Addr2,
  input  Addr1,
  input  Addr0,
  output out_10,
  output out_11,
  output out_12,
  output out_13,
  output out_14,
  output out_15,
  output out_16,
  output out_17
);

  wire not_1_out, not_2_out, not_3_out, not_4_out, not_5_out, not_6_out, not_7_out, not_8_out;

  not not_1 (not_1_out, Op2);
  not not_2 (not_2_out, Op1);
  not not_3 (not_3_out, Op0);
  not not_4 (not_4_out, Addr4);
  not not_5 (not_5_out, Addr3);
  not not_6 (not_6_out, Addr2);
  not not_7 (not_7_out, Addr1);
  not not_8 (not_8_out, Addr0);
  J_K_Flip_Flop j_k_ff_1 (.J(Op2), .clk(INPUT), .K(not_1_out), .Q(out_10));  // open: Qn, preset, en, reset
  J_K_Flip_Flop j_k_ff_2 (.J(Op1), .clk(INPUT), .K(not_2_out), .Q(out_11));  // open: Qn, preset, en, reset
  J_K_Flip_Flop j_k_ff_3 (.J(Op0), .clk(INPUT), .K(not_3_out), .Q(out_12));  // open: Qn, preset, en, reset
  J_K_Flip_Flop j_k_ff_4 (.J(Addr4), .clk(INPUT), .K(not_4_out), .Q(out_13));  // open: Qn, preset, en, reset
  J_K_Flip_Flop j_k_ff_5 (.J(Addr3), .clk(INPUT), .K(not_5_out), .Q(out_14));  // open: Qn, preset, en, reset
  J_K_Flip_Flop j_k_ff_6 (.J(Addr2), .clk(INPUT), .K(not_6_out), .Q(out_15));  // open: Qn, preset, en, reset
  J_K_Flip_Flop j_k_ff_7 (.J(Addr1), .clk(INPUT), .K(not_7_out), .Q(out_16));  // open: Qn, preset, en, reset
  J_K_Flip_Flop j_k_ff_8 (.J(Addr0), .clk(INPUT), .K(not_8_out), .Q(out_17));  // open: Qn, preset, en, reset
endmodule
