// Logisim project RAM8bits4bits.circ as structural Verilog: 7 circuits, main circuit RAM8bits
module _8bitCell (
  input  Clock,
  input  in_2,
  input  in_3,
  input  in_4,
  input  in_5,
  input  in_6,
  input  in_7,
  input  in_8,
  input  in_9,
  input  Mode,
  input  Adressed,
  output out_12,
  output out_13,
  output out_14,
  output out_15,
  output out_16,
  output out_17,
  output out_18,
  output out_19
);

  wire and_1_out, and_2_out, and_3_out, and_4_out, and_5_out, and_6_out, and_7_out, and_8_out, and_9_out,
       j_k_ff_1_q, j_k_ff_2_q, j_k_ff_3_q, j_k_ff_4_q, j_k_ff_5_q, j_k_ff_6_q, j_k_ff_7_q, j_k_ff_8_q,
       not_1_out, not_2_out, not_3_out, not_4_out, not_5_out, not_6_out, not_7_out, not_8_out, not_9_out;

  and and_1 (and_1_out, Adressed, in_2);
  and and_2 (and_2_out, Adressed, in_3);
  and and_3 (and_3_out, Adressed, in_4);
  and and_4 (and_4_out, in_5, Adressed);
  and and_5 (and_5_out, Adressed, in_6);
  and and_6 (and_6_out, Adressed, in_7);
  and and_7 (and_7_out, Adressed, in_8);
  and and_8 (and_8_out, Adressed, in_9);
  and and_9 (and_9_out, Clock, Adressed, Mode);
  not not_1 (not_1_out, and_1_out);
  not not_2 (not_2_out, and_2_out);
  not not_3 (not_3_out, and_3_out);
  not not_4 (not_4_out, and_4_out);
  not not_5 (not_5_out, and_5_out);
  not not_6 (not_6_out, and_6_out);
  not not_7 (not_7_out, and_7_out);
  not not_8 (not_8_out, and_8_out);
  J_K_Flip_Flop j_k_ff_1 (
    .J(and_1_out), .clk(and_9_out), .K(not_1_out), .Q(j_k_ff_1_q));  // open: Qn, preset, en, reset
  J_K_Flip_Flop j_k_ff_2 (
    .J(and_2_out), .clk(and_9_out), .K(not_2_out), .Q(j_k_ff_2_q));  // open: Qn, preset, en, reset
  J_K_Flip_Flop j_k_ff_3 (
    .J(and_3_out), .clk(and_9_out), .K(not_3_out), .Q(j_k_ff_3_q));  // open: Qn, preset, en, reset
  J_K_Flip_Flop j_k_ff_4 (
    .J(and_4_out), .clk(and_9_out), .K(not_4_out), .Q(j_k_ff_4_q));  // open: Qn, preset, en, reset
  J_K_Flip_Flop j_k_ff_5 (
    .J(and_5_out), .clk(and_9_out), .K(not_5_out), .Q(j_k_ff_5_q));  // open: Qn, preset, en, reset
  J_K_Flip_Flop j_k_ff_6 (
    .J(and_6_out), .clk(and_9_out), .K(not_6_out), .Q(j_k_ff_6_q));  // open: Qn, preset, en, reset
  J_K_Flip_Flop j_k_ff_7 (
    .J(and_7_out), .clk(and_9_out), .K(not_7_out), .Q(j_k_ff_7_q));  // open: Qn, preset, en, reset
  J_K_Flip_Flop j_k_ff_8 (
    .J(and_8_out), .clk(and_9_out), .K(not_8_out), .Q(j_k_ff_8_q));  // open: Qn, preset, en, reset
  not not_9 (not_9_out, Mode);
  and and_10 (out_12, not_9_out, j_k_ff_1_q, Adressed);
  and and_11 (out_13, j_k_ff_2_q, not_9_out, Adressed);
  and and_12 (out_14, j_k_ff_3_q, not_9_out, Adressed);
  and and_13 (out_15, j_k_ff_4_q, Adressed, not_9_out);
  and and_14 (out_16, j_k_ff_5_q, Adressed, not_9_out);
  and and_15 (out_17, j_k_ff_6_q, Adressed, not_9_out);
  and and_16 (out_18, j_k_ff_7_q, Adressed, not_9_out);
  and and_17 (out_19, j_k_ff_8_q, Adressed, not_9_out);
endmodule

module RAM8bits (
  input  CLK,
  input  in_2,
  input  ADDR,
  input  in_4,
  input  in_5,
  input  in_6,
  input  in_7,
  input  NIBBLE_1,
  input  in_9,
  input  in_10,
  input  NIBBLE_2,
  input  in_12,
  input  in_13,
  input  MODE,
  output out_15,
  output out_16,
  output out_17,
  output out_18,
  output out_19,
  output out_20,
  output out_21,
  output out_22
);

  wire and_5_out, and_6_out, and_7_out, and_8_out, and_9_out, and_10_out, and_11_out, and_12_out, and_13_out,
       and_14_out, and_15_out, and_16_out, and_17_out, and_18_out, and_19_out, and_20_out,
       n8bitcell_1_out_12, n8bitcell_1_out_13, n8bitcell_1_out_14, n8bitcell_1_out_15, n8bitcell_1_out_16,
       n8bitcell_1_out_17, n8bitcell_1_out_18, n8bitcell_1_out_19, n8bitcell_2_out_12, n8bitcell_2_out_13,
       n8bitcell_2_out_14, n8bitcell_2_out_15, n8bitcell_2_out_16, n8bitcell_2_out_17, n8bitcell_2_out_18,
       n8bitcell_2_out_19, n8bitcell_3_out_12, n8bitcell_3_out_13, n8bitcell_3_out_14, n8bitcell_3_out_15,
       n8bitcell_3_out_16, n8bitcell_3_out_17, n8bitcell_3_out_18, n8bitcell_3_out_19, n8bitcell_4_out_12,
       n8bitcell_4_out_13, n8bitcell_4_out_14, n8bitcell_4_out_15, n8bitcell_4_out_16, n8bitcell_4_out_17,
       n8bitcell_4_out_18, n8bitcell_4_out_19, n8bitcell_5_out_12, n8bitcell_5_out_13, n8bitcell_5_out_14,
       n8bitcell_5_out_15, n8bitcell_5_out_16, n8bitcell_5_out_17, n8bitcell_5_out_18, n8bitcell_5_out_19,
       n8bitcell_6_out_12, n8bitcell_6_out_13, n8bitcell_6_out_14, n8bitcell_6_out_15, n8bitcell_6_out_16,
       n8bitcell_6_out_17, n8bitcell_6_out_18, n8bitcell_6_out_19, n8bitcell_7_out_12, n8bitcell_7_out_13,
       n8bitcell_7_out_14, n8bitcell_7_out_15, n8bitcell_7_out_16, n8bitcell_7_out_17, n8bitcell_7_out_18,
       n8bitcell_7_out_19, n8bitcell_8_out_12, n8bitcell_8_out_13, n8bitcell_8_out_14, n8bitcell_8_out_15,
       n8bitcell_8_out_16, n8bitcell_8_out_17, n8bitcell_8_out_18, n8bitcell_8_out_19, n8bitcell_9_out_12,
       n8bitcell_9_out_13, n8bitcell_9_out_14, n8bitcell_9_out_15, n8bitcell_9_out_16, n8bitcell_9_out_17,
       n8bitcell_9_out_18, n8bitcell_9_out_19, n8bitcell_10_out_12, n8bitcell_10_out_13, n8bitcell_10_out_14,
       n8bitcell_10_out_15, n8bitcell_10_out_16, n8bitcell_10_out_17, n8bitcell_10_out_18,
       n8bitcell_10_out_19, n8bitcell_11_out_12, n8bitcell_11_out_13, n8bitcell_11_out_14,
       n8bitcell_11_out_15, n8bitcell_11_out_16, n8bitcell_11_out_17, n8bitcell_11_out_18,
       n8bitcell_11_out_19, n8bitcell_12_out_12, n8bitcell_12_out_13, n8bitcell_12_out_14,
       n8bitcell_12_out_15, n8bitcell_12_out_16, n8bitcell_12_out_17, n8bitcell_12_out_18,
       n8bitcell_12_out_19, n8bitcell_13_out_12, n8bitcell_13_out_13, n8bitcell_13_out_14,
       n8bitcell_13_out_15, n8bitcell_13_out_16, n8bitcell_13_out_17, n8bitcell_13_out_18,
       n8bitcell_13_out_19, n8bitcell_14_out_12, n8bitcell_14_out_13, n8bitcell_14_out_14,
       n8bitcell_14_out_15, n8bitcell_14_out_16, n8bitcell_14_out_17, n8bitcell_14_out_18,
       n8bitcell_14_out_19, n8bitcell_15_out_12, n8bitcell_15_out_13, n8bitcell_15_out_14,
       n8bitcell_15_out_15, n8bitcell_15_out_16, n8bitcell_15_out_17, n8bitcell_15_out_18,
       n8bitcell_15_out_19, n8bitcell_16_out_12, n8bitcell_16_out_13, n8bitcell_16_out_14,
       n8bitcell_16_out_15, n8bitcell_16_out_16, n8bitcell_16_out_17, n8bitcell_16_out_18,
       n8bitcell_16_out_19, not_1_out, not_2_out, not_3_out, not_4_out, not_5_out, not_6_out, not_7_out,
       not_8_out, not_9_out, not_10_out, not_11_out, not_12_out, not_13_out, not_14_out, not_15_out,
       not_16_out, not_17_out, not_18_out, not_19_out, not_20_out, not_21_out, not_22_out, not_23_out,
       not_24_out, not_25_out, not_26_out, not_27_out, not_28_out, not_29_out, not_30_out, not_31_out,
       not_32_out, or_3_out, or_5_out, or_6_out, or_7_out, or_8_out, or_9_out, or_10_out, or_13_out,
       or_14_out, or_15_out, or_16_out, or_18_out, or_19_out, or_20_out, or_22_out, or_23_out, or_24_out,
       or_25_out, or_27_out;

  // AND_Gate and_1 has open pins: in1=in_2, in2=ADDR, in3=in_4, in4=in_5, out=open
  // AND_Gate and_2 has open pins: in0=in_6, in1=in_7, in2=NIBBLE_1, in3=in_9, in4=in_10, out=open
  // AND_Gate and_3 has open pins: in0=CLK, out=open
  // AND_Gate and_4 has open pins: in0=NIBBLE_2, in1=in_12, in2=in_13, in4=MODE, out=open
  not not_1 (not_1_out, in_2);
  not not_2 (not_2_out, ADDR);
  not not_3 (not_3_out, in_4);
  and and_5 (and_5_out, not_1_out, not_2_out, not_3_out, in_5);
  not not_4 (not_4_out, in_2);
  not not_5 (not_5_out, ADDR);
  and and_6 (and_6_out, not_4_out, not_5_out, in_4, not_6_out);
  not not_6 (not_6_out, in_5);
  not not_7 (not_7_out, in_2);
  and and_7 (and_7_out, not_7_out, not_8_out, in_4, in_5);
  not not_8 (not_8_out, ADDR);
  not not_9 (not_9_out, in_2);
  not not_10 (not_10_out, in_4);
  not not_11 (not_11_out, in_5);
  not not_12 (not_12_out, in_2);
  not not_13 (not_13_out, in_4);
  and and_8 (and_8_out, not_12_out, ADDR, not_13_out, in_5);
  not not_14 (not_14_out, in_2);
  and and_9 (and_9_out, not_14_out, ADDR, in_4, in_5);
  not not_15 (not_15_out, ADDR);
  not not_16 (not_16_out, in_4);
  and and_10 (and_10_out, in_2, not_15_out, not_16_out, not_17_out);
  not not_17 (not_17_out, in_5);
  not not_18 (not_18_out, ADDR);
  not not_19 (not_19_out, in_4);
  and and_11 (and_11_out, in_2, not_18_out, not_19_out, in_5);
  not not_20 (not_20_out, ADDR);
  and and_12 (and_12_out, in_2, not_20_out, in_4, not_21_out);
  not not_21 (not_21_out, in_5);
  not not_22 (not_22_out, ADDR);
  and and_13 (and_13_out, in_2, not_22_out, in_4, in_5);
  not not_23 (not_23_out, in_4);
  and and_14 (and_14_out, in_2, ADDR, not_23_out, not_24_out);
  not not_24 (not_24_out, in_5);
  and and_15 (and_15_out, in_2, ADDR, not_25_out, in_5);
  not not_25 (not_25_out, in_4);
  and and_16 (and_16_out, in_2, ADDR, in_4, not_26_out);
  not not_26 (not_26_out, in_5);
  and and_17 (and_17_out, in_2, ADDR, in_4, in_5);
  not not_27 (not_27_out, in_2);
  and and_18 (and_18_out, not_27_out, ADDR, in_4, not_28_out);
  not not_28 (not_28_out, in_5);
  not not_29 (not_29_out, in_2);
  not not_30 (not_30_out, ADDR);
  and and_19 (and_19_out, not_29_out, not_30_out, not_31_out, not_32_out);
  not not_31 (not_31_out, in_4);
  not not_32 (not_32_out, in_5);
  _8bitCell u_8bitcell_1 (
    .Clock(CLK), .in_2(in_6), .in_3(in_7), .in_4(NIBBLE_1), .in_5(in_9), .in_6(in_10), .in_7(NIBBLE_2),
    .in_8(in_12), .in_9(in_13), .Mode(MODE), .Adressed(and_5_out), .out_12(n8bitcell_1_out_12),
    .out_13(n8bitcell_1_out_13), .out_14(n8bitcell_1_out_14), .out_15(n8bitcell_1_out_15),
    .out_16(n8bitcell_1_out_16), .out_17(n8bitcell_1_out_17), .out_18(n8bitcell_1_out_18),
    .out_19(n8bitcell_1_out_19));
  _8bitCell u_8bitcell_2 (
    .Clock(CLK), .in_2(in_6), .in_3(in_7), .in_4(NIBBLE_1), .in_5(in_9), .in_6(in_10), .in_7(NIBBLE_2),
    .in_8(in_12), .in_9(in_13), .Mode(MODE), .Adressed(and_6_out), .out_12(n8bitcell_2_out_12),
    .out_13(n8bitcell_2_out_13), .out_14(n8bitcell_2_out_14), .out_15(n8bitcell_2_out_15),
    .out_16(n8bitcell_2_out_16), .out_17(n8bitcell_2_out_17), .out_18(n8bitcell_2_out_18),
    .out_19(n8bitcell_2_out_19));
  _8bitCell u_8bitcell_3 (
    .Clock(CLK), .in_2(in_6), .in_3(in_7), .in_4(NIBBLE_1), .in_5(in_9), .in_6(in_10), .in_7(NIBBLE_2),
    .in_8(in_12), .in_9(in_13), .Mode(MODE), .Adressed(and_7_out), .out_12(n8bitcell_3_out_12),
    .out_13(n8bitcell_3_out_13), .out_14(n8bitcell_3_out_14), .out_15(n8bitcell_3_out_15),
    .out_16(n8bitcell_3_out_16), .out_17(n8bitcell_3_out_17), .out_18(n8bitcell_3_out_18),
    .out_19(n8bitcell_3_out_19));
  _8bitCell u_8bitcell_4 (
    .Clock(CLK), .in_2(in_6), .in_3(in_7), .in_4(NIBBLE_1), .in_5(in_9), .in_6(in_10), .in_7(NIBBLE_2),
    .in_8(in_12), .in_9(in_13), .Mode(MODE), .Adressed(and_20_out), .out_12(n8bitcell_4_out_12),
    .out_13(n8bitcell_4_out_13), .out_14(n8bitcell_4_out_14), .out_15(n8bitcell_4_out_15),
    .out_16(n8bitcell_4_out_16), .out_17(n8bitcell_4_out_17), .out_18(n8bitcell_4_out_18),
    .out_19(n8bitcell_4_out_19));
  and and_20 (and_20_out, not_9_out, ADDR, not_10_out, not_11_out);
  _8bitCell u_8bitcell_5 (
    .Clock(CLK), .in_2(in_6), .in_3(in_7), .in_4(NIBBLE_1), .in_5(in_9), .in_6(in_10), .in_7(NIBBLE_2),
    .in_8(in_12), .in_9(in_13), .Mode(MODE), .Adressed(and_8_out), .out_12(n8bitcell_5_out_12),
    .out_13(n8bitcell_5_out_13), .out_14(n8bitcell_5_out_14), .out_15(n8bitcell_5_out_15),
    .out_16(n8bitcell_5_out_16), .out_17(n8bitcell_5_out_17), .out_18(n8bitcell_5_out_18),
    .out_19(n8bitcell_5_out_19));
  _8bitCell u_8bitcell_6 (
    .Clock(CLK), .in_2(in_6), .in_3(in_7), .in_4(NIBBLE_1), .in_5(in_9), .in_6(in_10), .in_7(NIBBLE_2),
    .in_8(in_12), .in_9(in_13), .Mode(MODE), .Adressed(and_9_out), .out_12(n8bitcell_6_out_12),
    .out_13(n8bitcell_6_out_13), .out_14(n8bitcell_6_out_14), .out_15(n8bitcell_6_out_15),
    .out_16(n8bitcell_6_out_16), .out_17(n8bitcell_6_out_17), .out_18(n8bitcell_6_out_18),
    .out_19(n8bitcell_6_out_19));
  _8bitCell u_8bitcell_7 (
    .Clock(CLK), .in_2(in_6), .in_3(in_7), .in_4(NIBBLE_1), .in_5(in_9), .in_6(in_10), .in_7(NIBBLE_2),
    .in_8(in_12), .in_9(in_13), .Mode(MODE), .Adressed(and_10_out), .out_12(n8bitcell_7_out_12),
    .out_13(n8bitcell_7_out_13), .out_14(n8bitcell_7_out_14), .out_15(n8bitcell_7_out_15),
    .out_16(n8bitcell_7_out_16), .out_17(n8bitcell_7_out_17), .out_18(n8bitcell_7_out_18),
    .out_19(n8bitcell_7_out_19));
  _8bitCell u_8bitcell_8 (
    .Clock(CLK), .in_2(in_6), .in_3(in_7), .in_4(NIBBLE_1), .in_5(in_9), .in_6(in_10), .in_7(NIBBLE_2),
    .in_8(in_12), .in_9(in_13), .Mode(MODE), .Adressed(and_11_out), .out_12(n8bitcell_8_out_12),
    .out_13(n8bitcell_8_out_13), .out_14(n8bitcell_8_out_14), .out_15(n8bitcell_8_out_15),
    .out_16(n8bitcell_8_out_16), .out_17(n8bitcell_8_out_17), .out_18(n8bitcell_8_out_18),
    .out_19(n8bitcell_8_out_19));
  _8bitCell u_8bitcell_9 (
    .Clock(CLK), .in_2(in_6), .in_3(in_7), .in_4(NIBBLE_1), .in_5(in_9), .in_6(in_10), .in_7(NIBBLE_2),
    .in_8(in_12), .in_9(in_13), .Mode(MODE), .Adressed(and_12_out), .out_12(n8bitcell_9_out_12),
    .out_13(n8bitcell_9_out_13), .out_14(n8bitcell_9_out_14), .out_15(n8bitcell_9_out_15),
    .out_16(n8bitcell_9_out_16), .out_17(n8bitcell_9_out_17), .out_18(n8bitcell_9_out_18),
    .out_19(n8bitcell_9_out_19));
  _8bitCell u_8bitcell_10 (
    .Clock(CLK), .in_2(in_6), .in_3(in_7), .in_4(NIBBLE_1), .in_5(in_9), .in_6(in_10), .in_7(NIBBLE_2),
    .in_8(in_12), .in_9(in_13), .Mode(MODE), .Adressed(and_13_out), .out_12(n8bitcell_10_out_12),
    .out_13(n8bitcell_10_out_13), .out_14(n8bitcell_10_out_14), .out_15(n8bitcell_10_out_15),
    .out_16(n8bitcell_10_out_16), .out_17(n8bitcell_10_out_17), .out_18(n8bitcell_10_out_18),
    .out_19(n8bitcell_10_out_19));
  _8bitCell u_8bitcell_11 (
    .Clock(CLK), .in_2(in_6), .in_3(in_7), .in_4(NIBBLE_1), .in_5(in_9), .in_6(in_10), .in_7(NIBBLE_2),
    .in_8(in_12), .in_9(in_13), .Mode(MODE), .Adressed(and_14_out), .out_12(n8bitcell_11_out_12),
    .out_13(n8bitcell_11_out_13), .out_14(n8bitcell_11_out_14), .out_15(n8bitcell_11_out_15),
    .out_16(n8bitcell_11_out_16), .out_17(n8bitcell_11_out_17), .out_18(n8bitcell_11_out_18),
    .out_19(n8bitcell_11_out_19));
  _8bitCell u_8bitcell_12 (
    .Clock(CLK), .in_2(in_6), .in_3(in_7), .in_4(NIBBLE_1), .in_5(in_9), .in_6(in_10), .in_7(NIBBLE_2),
    .in_8(in_12), .in_9(in_13), .Mode(MODE), .Adressed(and_15_out), .out_12(n8bitcell_12_out_12),
    .out_13(n8bitcell_12_out_13), .out_14(n8bitcell_12_out_14), .out_15(n8bitcell_12_out_15),
    .out_16(n8bitcell_12_out_16), .out_17(n8bitcell_12_out_17), .out_18(n8bitcell_12_out_18),
    .out_19(n8bitcell_12_out_19));
  _8bitCell u_8bitcell_13 (
    .Clock(CLK), .in_2(in_6), .in_3(in_7), .in_4(NIBBLE_1), .in_5(in_9), .in_6(in_10), .in_7(NIBBLE_2),
    .in_8(in_12), .in_9(in_13), .Mode(MODE), .Adressed(and_16_out), .out_12(n8bitcell_13_out_12),
    .out_13(n8bitcell_13_out_13), .out_14(n8bitcell_13_out_14), .out_15(n8bitcell_13_out_15),
    .out_16(n8bitcell_13_out_16), .out_17(n8bitcell_13_out_17), .out_18(n8bitcell_13_out_18),
    .out_19(n8bitcell_13_out_19));
  _8bitCell u_8bitcell_14 (
    .Clock(CLK), .in_2(in_6), .in_3(in_7), .in_4(NIBBLE_1), .in_5(in_9), .in_6(in_10), .in_7(NIBBLE_2),
    .in_8(in_12), .in_9(in_13), .Mode(MODE), .Adressed(and_17_out), .out_12(n8bitcell_14_out_12),
    .out_13(n8bitcell_14_out_13), .out_14(n8bitcell_14_out_14), .out_15(n8bitcell_14_out_15),
    .out_16(n8bitcell_14_out_16), .out_17(n8bitcell_14_out_17), .out_18(n8bitcell_14_out_18),
    .out_19(n8bitcell_14_out_19));
  _8bitCell u_8bitcell_15 (
    .Clock(CLK), .in_2(in_6), .in_3(in_7), .in_4(NIBBLE_1), .in_5(in_9), .in_6(in_10), .in_7(NIBBLE_2),
    .in_8(in_12), .in_9(in_13), .Mode(MODE), .Adressed(and_18_out), .out_12(n8bitcell_15_out_12),
    .out_13(n8bitcell_15_out_13), .out_14(n8bitcell_15_out_14), .out_15(n8bitcell_15_out_15),
    .out_16(n8bitcell_15_out_16), .out_17(n8bitcell_15_out_17), .out_18(n8bitcell_15_out_18),
    .out_19(n8bitcell_15_out_19));
  _8bitCell u_8bitcell_16 (
    .Clock(CLK), .in_2(in_6), .in_3(in_7), .in_4(NIBBLE_1), .in_5(in_9), .in_6(in_10), .in_7(NIBBLE_2),
    .in_8(in_12), .in_9(in_13), .Mode(MODE), .Adressed(and_19_out), .out_12(n8bitcell_16_out_12),
    .out_13(n8bitcell_16_out_13), .out_14(n8bitcell_16_out_14), .out_15(n8bitcell_16_out_15),
    .out_16(n8bitcell_16_out_16), .out_17(n8bitcell_16_out_17), .out_18(n8bitcell_16_out_18),
    .out_19(n8bitcell_16_out_19));
  or or_1 (out_15, n8bitcell_14_out_12, n8bitcell_13_out_12, n8bitcell_12_out_12, n8bitcell_11_out_12, n8bitcell_10_out_12, n8bitcell_9_out_12, n8bitcell_8_out_12, n8bitcell_7_out_12, n8bitcell_5_out_12, n8bitcell_4_out_12, n8bitcell_3_out_12, n8bitcell_2_out_12, n8bitcell_1_out_12, n8bitcell_6_out_12, n8bitcell_15_out_12, n8bitcell_16_out_12);
  or or_2 (out_16, n8bitcell_16_out_13, n8bitcell_15_out_13, n8bitcell_14_out_13, n8bitcell_13_out_13, n8bitcell_12_out_13, n8bitcell_11_out_13, n8bitcell_10_out_13, n8bitcell_9_out_13, n8bitcell_7_out_13, n8bitcell_6_out_13, n8bitcell_5_out_13, n8bitcell_4_out_13, n8bitcell_3_out_13, n8bitcell_2_out_13, n8bitcell_1_out_13, n8bitcell_8_out_13);
  or or_3 (or_3_out, n8bitcell_14_out_14, n8bitcell_13_out_14, n8bitcell_12_out_14, or_7_out);
  or or_4 (out_17, n8bitcell_16_out_14, n8bitcell_15_out_14, or_3_out);
  or or_5 (or_5_out, n8bitcell_3_out_14, n8bitcell_2_out_14, n8bitcell_1_out_14);
  or or_6 (or_6_out, n8bitcell_7_out_14, n8bitcell_6_out_14, n8bitcell_5_out_14, n8bitcell_4_out_14, or_5_out);
  or or_7 (or_7_out, n8bitcell_11_out_14, n8bitcell_10_out_14, n8bitcell_9_out_14, n8bitcell_8_out_14, or_6_out);
  or or_8 (or_8_out, n8bitcell_5_out_15, n8bitcell_4_out_15, n8bitcell_3_out_15, n8bitcell_2_out_15, n8bitcell_1_out_15);
  or or_9 (or_9_out, n8bitcell_9_out_15, n8bitcell_8_out_15, n8bitcell_7_out_15, n8bitcell_6_out_15, or_8_out);
  or or_10 (or_10_out, n8bitcell_13_out_15, n8bitcell_12_out_15, n8bitcell_11_out_15, n8bitcell_10_out_15, or_9_out);
  or or_11 (out_18, n8bitcell_16_out_15, n8bitcell_15_out_15, n8bitcell_14_out_15, or_10_out);
  or or_12 (out_19, n8bitcell_16_out_16, n8bitcell_15_out_16, n8bitcell_14_out_16, n8bitcell_13_out_16, or_15_out);
  or or_13 (or_13_out, n8bitcell_4_out_16, n8bitcell_3_out_16, n8bitcell_2_out_16, n8bitcell_1_out_16);
  or or_14 (or_14_out, n8bitcell_8_out_16, n8bitcell_7_out_16, n8bitcell_6_out_16, n8bitcell_5_out_16, or_13_out);
  or or_15 (or_15_out, n8bitcell_12_out_16, n8bitcell_11_out_16, n8bitcell_10_out_16, n8bitcell_9_out_16, or_14_out);
  or or_16 (or_16_out, n8bitcell_12_out_17, n8bitcell_11_out_17, n8bitcell_10_out_17, n8bitcell_9_out_17, or_19_out);
  or or_17 (out_20, n8bitcell_16_out_17, n8bitcell_15_out_17, n8bitcell_14_out_17, n8bitcell_13_out_17, or_16_out);
  or or_18 (or_18_out, n8bitcell_4_out_17, n8bitcell_3_out_17, n8bitcell_2_out_17, n8bitcell_1_out_17);
  or or_19 (or_19_out, n8bitcell_8_out_17, n8bitcell_7_out_17, n8bitcell_6_out_17, n8bitcell_5_out_17, or_18_out);
  or or_20 (or_20_out, n8bitcell_12_out_18, n8bitcell_11_out_18, n8bitcell_10_out_18, n8bitcell_9_out_18, or_23_out);
  or or_21 (out_21, n8bitcell_16_out_18, n8bitcell_15_out_18, n8bitcell_14_out_18, n8bitcell_13_out_18, or_20_out);
  or or_22 (or_22_out, n8bitcell_3_out_18, n8bitcell_2_out_18, n8bitcell_1_out_18, n8bitcell_4_out_18);
  or or_23 (or_23_out, n8bitcell_8_out_18, n8bitcell_7_out_18, n8bitcell_6_out_18, n8bitcell_5_out_18, or_22_out);
  or or_24 (or_24_out, n8bitcell_8_out_19, n8bitcell_7_out_19, n8bitcell_6_out_19, n8bitcell_5_out_19, or_27_out);
  or or_25 (or_25_out, n8bitcell_12_out_19, n8bitcell_11_out_19, n8bitcell_10_out_19, n8bitcell_9_out_19, or_24_out);
  or or_26 (out_22, n8bitcell_16_out_19, n8bitcell_15_out_19, n8bitcell_14_out_19, n8bitcell_13_out_19, or_25_out);
  or or_27 (or_27_out, n8bitcell_4_out_19, n8bitcell_3_out_19, n8bitcell_2_out_19, n8bitcell_1_out_19);

  // Notes on the sheet:
  //   0001
  //   0100
  //   0101
  //   0111
  //   1001
  //   1010
  //   1011
  //   1100
  //   1101
  //   1110
  //   0001
  //   0010
  //   0011
  //   1000
  //   1111
  //   0110
  //   0000
endmodule

module Registers (
  input  in_1,
  input  in_2,
  input  in_3,
  input  in_4,
  input  in_5,
  input  in_6,
  input  in_7,
  input  in_8,
  input  in_9,
  input  in_10,
  input  in_11,
  output out_12,
  output out_13,
  output out_14,
  output out_15,
  output out_16,
  output out_17,
  output out_18,
  output out_19
);

  wire n8bitcell_1_out_12, n8bitcell_1_out_13, n8bitcell_1_out_14, n8bitcell_1_out_15, n8bitcell_1_out_16,
       n8bitcell_1_out_17, n8bitcell_1_out_18, n8bitcell_1_out_19, n8bitcell_2_out_12, n8bitcell_2_out_13,
       n8bitcell_2_out_14, n8bitcell_2_out_15, n8bitcell_2_out_16, n8bitcell_2_out_17, n8bitcell_2_out_18,
       n8bitcell_2_out_19, not_1_out;

  not not_1 (not_1_out, in_2);
  _8bitCell u_8bitcell_1 (
    .Clock(in_1), .in_2(in_3), .in_3(in_4), .in_4(in_5), .in_5(in_6), .in_6(in_7), .in_7(in_7), .in_8(in_9),
    .in_9(in_10), .Mode(in_11), .Adressed(in_2), .out_12(n8bitcell_1_out_12), .out_13(n8bitcell_1_out_13),
    .out_14(n8bitcell_1_out_14), .out_15(n8bitcell_1_out_15), .out_16(n8bitcell_1_out_16),
    .out_17(n8bitcell_1_out_17), .out_18(n8bitcell_1_out_18), .out_19(n8bitcell_1_out_19));
  _8bitCell u_8bitcell_2 (
    .Clock(in_1), .in_2(in_3), .in_3(in_4), .in_4(in_5), .in_5(in_6), .in_6(in_7), .in_7(in_7), .in_8(in_9),
    .in_9(in_10), .Mode(in_11), .Adressed(not_1_out), .out_12(n8bitcell_2_out_12),
    .out_13(n8bitcell_2_out_13), .out_14(n8bitcell_2_out_14), .out_15(n8bitcell_2_out_15),
    .out_16(n8bitcell_2_out_16), .out_17(n8bitcell_2_out_17), .out_18(n8bitcell_2_out_18),
    .out_19(n8bitcell_2_out_19));
  or or_1 (out_12, n8bitcell_1_out_12, n8bitcell_2_out_12);
  or or_2 (out_13, n8bitcell_1_out_13, n8bitcell_2_out_13);
  or or_3 (out_14, n8bitcell_1_out_14, n8bitcell_2_out_14);
  or or_4 (out_15, n8bitcell_1_out_15, n8bitcell_2_out_15);
  or or_5 (out_16, n8bitcell_1_out_16, n8bitcell_2_out_16);
  or or_6 (out_17, n8bitcell_1_out_17, n8bitcell_2_out_17);
  or or_7 (out_19, n8bitcell_1_out_19, n8bitcell_2_out_19);
  or or_8 (out_18, n8bitcell_1_out_18, n8bitcell_2_out_18);
  Register_Block register_block_1 ();  // open: MODE, CLK, in_3, in_4, in_5, in_6, in_7, in_8, in_9, in_10, in_11, in_12, in_13, out_14, out_15

  assign in_8 = in_7;
endmodule

module PC_Register (
  input  in_1,
  input  in_2,
  input  in_3,
  input  in_4,
  input  in_5,
  input  in_6,
  input  in_7,
  input  in_8,
  input  in_9,
  output out_10,
  output out_11,
  output out_12,
  output out_13,
  output out_14,
  output out_15,
  output out_16,
  output out_17
);

  wire not_1_out;

  not not_1 (not_1_out, 1'b0);
  _8bitCell u_8bitcell_1 (
    .Clock(in_1), .in_2(in_2), .in_3(in_3), .in_4(in_4), .in_5(in_5), .in_6(in_6), .in_7(in_7), .in_8(in_8),
    .in_9(in_9), .Mode(not_1_out), .Adressed(not_1_out), .out_12(out_10), .out_13(out_11), .out_14(out_12),
    .out_15(out_13), .out_16(out_14), .out_17(out_15), .out_18(out_16), .out_19(out_17));
endmodule

module Register_Block (
  input  MODE,
  input  CLK,
  input  in_3,
  input  in_4,
  input  in_5,
  input  in_6,
  input  in_7,
  input  in_8,
  input  in_9,
  input  in_10,
  input  in_11,
  input  in_12,
  input  in_13,
  output [7:0] out_14,
  output [7:0] out_15
);

  wire and_1_out, not_1_out, not_3_out, or_1_out, or_2_out, or_3_out, or_4_out;
  wire [7:0] n8bitcellnoretain_1_out_19, n8bitcellnoretain_2_out_19;

  not not_1 (not_1_out, in_5);
  or or_1 (or_1_out, in_4, in_3);
  // NOT_Gate not_2 has open pins: in=MODE, out=open
  not not_3 (not_3_out, MODE);
  and and_1 (and_1_out, not_3_out, or_2_out);
  or or_2 (or_2_out, in_3, in_4);
  buf or_3 (or_3_out, not_1_out);  // OR_Gate
  buf or_4 (or_4_out, in_5);  // OR_Gate
  _8bitCellNoRetain u_8bitcellnoretain_1 (
    .Clock(CLK), .in_2(in_6), .in_3(in_7), .in_4(in_8), .in_5(in_9), .in_6(in_10), .in_7(in_11),
    .in_8(in_12), .in_9(in_13), .Mode(MODE), .Adressed(or_4_out), .out_12(n8bitcellnoretain_1_out_19[7]),
    .out_13(n8bitcellnoretain_1_out_19[6]), .out_14(n8bitcellnoretain_1_out_19[5]),
    .out_15(n8bitcellnoretain_1_out_19[4]), .out_16(n8bitcellnoretain_1_out_19[3]),
    .out_17(n8bitcellnoretain_1_out_19[2]), .out_18(n8bitcellnoretain_1_out_19[1]),
    .out_19(n8bitcellnoretain_1_out_19[0]));
  _8bitCellNoRetain u_8bitcellnoretain_2 (
    .Clock(CLK), .in_2(in_6), .in_3(in_7), .in_4(in_8), .in_5(in_9), .in_6(in_10), .in_7(in_11),
    .in_8(in_12), .in_9(in_13), .Mode(MODE), .Adressed(or_3_out), .out_12(n8bitcellnoretain_2_out_19[7]),
    .out_13(n8bitcellnoretain_2_out_19[6]), .out_14(n8bitcellnoretain_2_out_19[5]),
    .out_15(n8bitcellnoretain_2_out_19[4]), .out_16(n8bitcellnoretain_2_out_19[3]),
    .out_17(n8bitcellnoretain_2_out_19[2]), .out_18(n8bitcellnoretain_2_out_19[1]),
    .out_19(n8bitcellnoretain_2_out_19[0]));
  Multiplexer #(.width(8)) multiplexer_1 (
    .in0(n8bitcellnoretain_2_out_19), .in1(n8bitcellnoretain_1_out_19), .out(out_14), .sel(in_3));  // open: en
  Multiplexer #(.width(8)) multiplexer_2 (
    .in0(n8bitcellnoretain_2_out_19), .in1(n8bitcellnoretain_1_out_19), .out(out_15), .sel(in_4));  // open: en

  // Notes on the sheet:
  //   Reg 2
  //   Reg 1
  //   Write reg
endmodule

module _8bitCellNoRetain (
  input  Clock,
  input  in_2,
  input  in_3,
  input  in_4,
  input  in_5,
  input  in_6,
  input  in_7,
  input  in_8,
  input  in_9,
  input  Mode,
  input  Adressed,
  output out_12,
  output out_13,
  output out_14,
  output out_15,
  output out_16,
  output out_17,
  output out_18,
  output out_19
);

  wire and_1_out, and_2_out, and_3_out, and_4_out, and_5_out, and_6_out, and_7_out, and_8_out, and_9_out,
       j_k_ff_1_q, j_k_ff_2_q, j_k_ff_3_q, j_k_ff_4_q, j_k_ff_5_q, j_k_ff_6_q, j_k_ff_7_q, j_k_ff_8_q,
       not_1_out, not_2_out, not_3_out, not_4_out, not_5_out, not_6_out, not_7_out, not_8_out, not_9_out,
       or_1_out;

  and and_1 (and_1_out, 1'b1, in_2);
  and and_2 (and_2_out, 1'b1, in_3);
  and and_3 (and_3_out, 1'b1, in_4);
  and and_4 (and_4_out, in_5, 1'b1);
  and and_5 (and_5_out, 1'b1, in_6);
  and and_6 (and_6_out, 1'b1, in_7);
  and and_7 (and_7_out, 1'b1, in_8);
  and and_8 (and_8_out, 1'b1, in_9);
  and and_9 (and_9_out, Clock, Adressed, Mode);
  not not_1 (not_1_out, and_1_out);
  not not_2 (not_2_out, and_2_out);
  not not_3 (not_3_out, and_3_out);
  not not_4 (not_4_out, and_4_out);
  not not_5 (not_5_out, and_5_out);
  not not_6 (not_6_out, and_6_out);
  not not_7 (not_7_out, and_7_out);
  not not_8 (not_8_out, and_8_out);
  J_K_Flip_Flop j_k_ff_1 (
    .J(and_1_out), .clk(and_9_out), .K(not_1_out), .Q(j_k_ff_1_q));  // open: Qn, preset, en, reset
  J_K_Flip_Flop j_k_ff_2 (
    .J(and_2_out), .clk(and_9_out), .K(not_2_out), .Q(j_k_ff_2_q));  // open: Qn, preset, en, reset
  J_K_Flip_Flop j_k_ff_3 (
    .J(and_3_out), .clk(and_9_out), .K(not_3_out), .Q(j_k_ff_3_q));  // open: Qn, preset, en, reset
  J_K_Flip_Flop j_k_ff_4 (
    .J(and_4_out), .clk(and_9_out), .K(not_4_out), .Q(j_k_ff_4_q));  // open: Qn, preset, en, reset
  J_K_Flip_Flop j_k_ff_5 (
    .J(and_5_out), .clk(and_9_out), .K(not_5_out), .Q(j_k_ff_5_q));  // open: Qn, preset, en, reset
  J_K_Flip_Flop j_k_ff_6 (
    .J(and_6_out), .clk(and_9_out), .K(not_6_out), .Q(j_k_ff_6_q));  // open: Qn, preset, en, reset
  J_K_Flip_Flop j_k_ff_7 (
    .J(and_7_out), .clk(and_9_out), .K(not_7_out), .Q(j_k_ff_7_q));  // open: Qn, preset, en, reset
  J_K_Flip_Flop j_k_ff_8 (
    .J(and_8_out), .clk(and_9_out), .K(not_8_out), .Q(j_k_ff_8_q));  // open: Qn, preset, en, reset
  or or_1 (or_1_out, Mode, not_9_out);
  not not_9 (not_9_out, Mode);
  and and_10 (out_12, or_1_out, j_k_ff_1_q, 1'b1);
  and and_11 (out_13, j_k_ff_2_q, or_1_out, 1'b1);
  and and_12 (out_14, j_k_ff_3_q, or_1_out, 1'b1);
  and and_13 (out_15, j_k_ff_4_q, 1'b1, or_1_out);
  and and_14 (out_16, j_k_ff_5_q, 1'b1, or_1_out);
  and and_15 (out_17, j_k_ff_6_q, 1'b1, or_1_out);
  and and_16 (out_18, j_k_ff_7_q, 1'b1, or_1_out);
  and and_17 (out_19, j_k_ff_8_q, 1'b1, or_1_out);
endmodule

module PC (
  input  INPUT,
  input  Op2,
  input  Op1,
  input  Op0,
  input  Addr4,
  input  Addr3,
  input  Addr2,
  input  Addr1,
  input  Addr0,
  output out_10,
  output out_11,
  output out_12,
  output out_13,
  output out_14,
  output out_15,
  output out_16,
  output out_17
);

  wire not_1_out, not_2_out, not_3_out, not_4_out, not_5_out, not_6_out, not_7_out, not_8_out;

  not not_1 (not_1_out, Op2);
  not not_2 (not_2_out, Op1);
  not not_3 (not_3_out, Op0);
  not not_4 (not_4_out, Addr4);
  not not_5 (not_5_out, Addr3);
  not not_6 (not_6_out, Addr2);
  not not_7 (not_7_out, Addr1);
  not not_8 (not_8_out, Addr0);
  J_K_Flip_Flop j_k_ff_1 (.J(Op2), .clk(INPUT), .K(not_1_out), .Q(out_10));  // open: Qn, preset, en, reset
  J_K_Flip_Flop j_k_ff_2 (.J(Op1), .clk(INPUT), .K(not_2_out), .Q(out_11));  // open: Qn, preset, en, reset
  J_K_Flip_Flop j_k_ff_3 (.J(Op0), .clk(INPUT), .K(not_3_out), .Q(out_12));  // open: Qn, preset, en, reset
  J_K_Flip_Flop j_k_ff_4 (.J(Addr4), .clk(INPUT), .K(not_4_out), .Q(out_13));  // open: Qn, preset, en, reset
  J_K_Flip_Flop j_k_ff_5 (.J(Addr3), .clk(INPUT), .K(not_5_out), .Q(out_14));  // open: Qn, preset, en, reset
  J_K_Flip_Flop j_k_ff_6 (.J(Addr2), .clk(INPUT), .K(not_6_out), .Q(out_15));  // open: Qn, preset, en, reset
  J_K_Flip_Flop j_k_ff_7 (.J(Addr1), .clk(INPUT), .K(not_7_out), .Q(out_16));  // open: Qn, preset, en, reset
  J_K_Flip_Flop j_k_ff_8 (.J(Addr0), .clk(INPUT), .K(not_8_out), .Q(out_17));  // open: Qn, preset, en, reset
endmodule
