// Logisim project Global.circ as structural Verilog
module main (
  input  _1,
  input  _2,
  input  _3,
  input  _4,
  input  _5,
  input  _6,
  input  _7,
  input  _8,
  input  _9,
  input  _0,
  input  Enter,
  input  in_12
);

  wire and_1_out, and_2_out, and_3_out, and_4_out, Bits_are_inversed_here_output_0,
       Bits_are_inversed_here_output_1, Bits_are_inversed_here_output_2, Bits_are_inversed_here_output_3,
       Bits_are_inversed_here_output_4, Bits_are_inversed_here_output_5, Bits_are_inversed_here_output_6,
       Bits_are_inversed_here_output_7, Bits_are_inversed_here_zero, clock_1_out, j_k_ff_1_q,
       main_3_alu_op_1, main_3_alu_op_2, main_3_branch, main_3_finished_cycle, main_3_memread,
       main_3_memtoreg, main_3_out_11, main_3_out_16, main_3_print, main_3_read_keypad, main_3_regwri,
       main_5_add_sub, main_5_mult, not_1_out, not_2_out, not_3_out, not_4_out, or_1_out, or_2_out,
       ram8bits_1_out_15, ram8bits_1_out_16, ram8bits_1_out_17, ram8bits_1_out_18, ram8bits_1_out_19,
       ram8bits_1_out_20, ram8bits_1_out_21, ram8bits_1_out_22;
  wire [2:0] main2_1_lb, main2_1_lb_2;
  wire [3:0] main2_1_m, main2_1_m_2;
  wire [7:0] adder_1_out, keypad_1_out_19, main_1_out_17, main_2_out_17, main_4_out_17, main_6_out_10,
       main_7_out_17, multiplexer_1_out, multiplexer_2_out, multiplexer_3_out, multiplexer_4_out,
       multiplexer_5_out, PC_out_17, ram8bits_2_out_22, register_block_1_out_14, register_block_1_out_15;

  RAM8bits ram8bits_1 (
    .CLK(clock_1_out), .in_2(PC_out_17[3]), .ADDR(PC_out_17[2]), .in_4(PC_out_17[1]), .in_5(PC_out_17[0]),
    .in_6(1'b0), .in_7(1'b0), .NIBBLE_1(1'b0), .in_9(1'b0), .in_10(1'b0), .NIBBLE_2(1'b0), .in_12(1'b0),
    .in_13(1'b0), .MODE(1'b0), .out_15(ram8bits_1_out_15), .out_16(ram8bits_1_out_16),
    .out_17(ram8bits_1_out_17), .out_18(ram8bits_1_out_18), .out_19(ram8bits_1_out_19),
    .out_20(ram8bits_1_out_20), .out_21(ram8bits_1_out_21), .out_22(ram8bits_1_out_22));
  and and_1 (and_1_out, and_2_out, main_3_finished_cycle, main_3_finished_cycle, main_3_finished_cycle);
  IR_main PC (
    .INPUT(and_1_out), .Op2(multiplexer_1_out[7]), .Op1(multiplexer_1_out[6]), .Op0(multiplexer_1_out[5]),
    .Addr4(multiplexer_1_out[4]), .Addr3(multiplexer_1_out[3]), .Addr2(multiplexer_1_out[2]),
    .Addr1(multiplexer_1_out[1]), .Addr0(multiplexer_1_out[0]), .out_10(PC_out_17[7]), .out_11(PC_out_17[6]),
    .out_12(PC_out_17[5]), .out_13(PC_out_17[4]), .out_14(PC_out_17[3]), .out_15(PC_out_17[2]),
    .out_16(PC_out_17[1]), .out_17(PC_out_17[0]));
  Clock clock_1 (.out(clock_1_out));
  Keypad keypad_1 (
    .in_11(Enter), .in_1(_1), .in_4(_4), .in_7(_7), .in_2(_2), .in_5(_5), .in_8(_8), .in_10(_0), .in_3(_3),
    .in_6(_6), .in_9(_9), .out_12(keypad_1_out_19[7]), .out_13(keypad_1_out_19[6]),
    .out_14(keypad_1_out_19[5]), .out_15(keypad_1_out_19[4]), .out_16(keypad_1_out_19[3]),
    .out_17(keypad_1_out_19[2]), .out_18(keypad_1_out_19[1]), .out_19(keypad_1_out_19[0]));
  J_K_Flip_Flop j_k_ff_1 (
    .J(main_3_out_11), .clk(clock_1_out), .K(not_1_out), .Q(j_k_ff_1_q));  // open: Qn, preset, en, reset
  not not_1 (not_1_out, main_3_out_11);
  IR_main main_1 (
    .INPUT(clock_1_out), .Op2(ram8bits_1_out_15), .Op1(ram8bits_1_out_16), .Op0(ram8bits_1_out_17),
    .Addr4(ram8bits_1_out_18), .Addr3(ram8bits_1_out_19), .Addr2(ram8bits_1_out_20),
    .Addr1(ram8bits_1_out_21), .Addr0(ram8bits_1_out_22), .out_10(main_1_out_17[7]),
    .out_11(main_1_out_17[6]), .out_12(main_1_out_17[5]), .out_13(main_1_out_17[4]),
    .out_14(main_1_out_17[3]), .out_15(main_1_out_17[2]), .out_16(main_1_out_17[1]), .out_17(main_1_out_17[0]));
  Multiplexer #(.width(8)) multiplexer_1 (
    .in0(main_4_out_17), .in1({4'b0000, main_1_out_17[5:2]}), .out(multiplexer_1_out), .sel(or_1_out));  // open: en
  and and_2 (and_2_out, j_k_ff_1_q, clock_1_out);
  IR_main main_2 (
    .INPUT(and_2_out), .Op2(keypad_1_out_19[7]), .Op1(keypad_1_out_19[6]), .Op0(keypad_1_out_19[5]),
    .Addr4(keypad_1_out_19[4]), .Addr3(keypad_1_out_19[3]), .Addr2(keypad_1_out_19[2]),
    .Addr1(keypad_1_out_19[1]), .Addr0(keypad_1_out_19[0]), .out_10(main_2_out_17[7]),
    .out_11(main_2_out_17[6]), .out_12(main_2_out_17[5]), .out_13(main_2_out_17[4]),
    .out_14(main_2_out_17[3]), .out_15(main_2_out_17[2]), .out_16(main_2_out_17[1]), .out_17(main_2_out_17[0]));
  Adder adder_1 (.a(PC_out_17), .b(8'h1), .out(adder_1_out));  // open: cin, cout
  or or_1 (or_1_out, and_4_out, and_3_out);
  not not_2 (not_2_out, main_3_read_keypad);
  Multiplexer #(.width(8)) multiplexer_2 (
    .in0(main_2_out_17), .in1(multiplexer_4_out), .out(multiplexer_2_out), .sel(not_2_out));  // open: en
  and and_3 (and_3_out, not_3_out, Bits_are_inversed_here_zero, main_3_branch);
  not not_3 (not_3_out, main_1_out_17[0]);
  CU_main main_3 (
    .in_1(clock_1_out), .Op_1(main_1_out_17[7]), .Op_2(main_1_out_17[6]), .Fn_2(main_1_out_17[4]),
    .Fn_3(main_1_out_17[3]), .Fn_4(main_1_out_17[2]), .IN_1_2(main_1_out_17[1]), .IN_2(main_1_out_17[0]),
    .MemToReg(main_3_memtoreg), .RegWri(main_3_regwri), .MemRead(main_3_memread), .out_16(main_3_out_16),
    .Branch(main_3_branch), .ALU_OP_1(main_3_alu_op_1), .ALU_OP_2(main_3_alu_op_2),
    .Read_Keypad(main_3_read_keypad), .Print(main_3_print), .in_10(3'b001),
    .Finished_Cycle(main_3_finished_cycle), .out_11(main_3_out_11));  // open: Fn_1, ALU_SRC
  Register_Block register_block_1 (
    .MODE(main_3_regwri), .CLK(and_2_out), .in_3(main_1_out_17[1]), .in_4(main_1_out_17[0]),
    .in_5(main_1_out_17[1]), .in_6(multiplexer_2_out[7]), .in_7(multiplexer_2_out[6]),
    .in_8(multiplexer_2_out[5]), .in_9(multiplexer_2_out[4]), .in_10(multiplexer_2_out[3]),
    .in_11(multiplexer_2_out[2]), .in_12(multiplexer_2_out[1]), .in_13(multiplexer_2_out[0]),
    .out_14(register_block_1_out_14), .out_15(register_block_1_out_15));
  Multiplexer #(.width(8)) multiplexer_3 (
    .in0(register_block_1_out_15), .in1({8{1'b0}}), .out(multiplexer_3_out), .sel(main_3_branch));  // open: en
  IR_main main_4 (
    .INPUT(and_2_out), .Op2(adder_1_out[7]), .Op1(adder_1_out[6]), .Op0(adder_1_out[5]),
    .Addr4(adder_1_out[4]), .Addr3(adder_1_out[3]), .Addr2(adder_1_out[2]), .Addr1(adder_1_out[1]),
    .Addr0(adder_1_out[0]), .out_10(main_4_out_17[7]), .out_11(main_4_out_17[6]), .out_12(main_4_out_17[5]),
    .out_13(main_4_out_17[4]), .out_14(main_4_out_17[3]), .out_15(main_4_out_17[2]),
    .out_16(main_4_out_17[1]), .out_17(main_4_out_17[0]));
  ALUControlblock_main main_5 (
    .ALUOp1(main_3_alu_op_1), .ALUOp0(main_3_alu_op_2), .Fn2(main_1_out_17[4]), .Fn1(main_1_out_17[3]),
    .Fn0(main_1_out_17[2]), .Add_Sub(main_5_add_sub), .Mult(main_5_mult));
  Multiplexer #(.width(8)) multiplexer_4 (
    .in0(main_6_out_10), .in1(ram8bits_2_out_22), .out(multiplexer_4_out), .sel(main_3_memtoreg));  // open: en
  IR_main main_6 (
    .INPUT(and_2_out), .Op2(Bits_are_inversed_here_output_0), .Op1(Bits_are_inversed_here_output_1),
    .Op0(Bits_are_inversed_here_output_2), .Addr4(Bits_are_inversed_here_output_3),
    .Addr3(Bits_are_inversed_here_output_4), .Addr2(Bits_are_inversed_here_output_5),
    .Addr1(Bits_are_inversed_here_output_6), .Addr0(Bits_are_inversed_here_output_7),
    .out_10(main_6_out_10[0]), .out_11(main_6_out_10[1]), .out_12(main_6_out_10[2]),
    .out_13(main_6_out_10[3]), .out_14(main_6_out_10[4]), .out_15(main_6_out_10[5]),
    .out_16(main_6_out_10[6]), .out_17(main_6_out_10[7]));
  _8bitALU Bits_are_inversed_here (
    .Input_A0(register_block_1_out_14[0]), .Input_A1(register_block_1_out_14[1]),
    .Input_A2(register_block_1_out_14[2]), .Input_A3(register_block_1_out_14[3]),
    .Input_A4(register_block_1_out_14[4]), .Input_A5(register_block_1_out_14[5]),
    .Input_A6(register_block_1_out_14[6]), .Input_A7(register_block_1_out_14[7]),
    .Input_B0(multiplexer_3_out[0]), .Input_B1(multiplexer_3_out[1]), .Input_B2(multiplexer_3_out[2]),
    .Input_B3(multiplexer_3_out[3]), .Input_B4(multiplexer_3_out[4]), .Input_B5(multiplexer_3_out[5]),
    .Input_B6(multiplexer_3_out[6]), .Input_B7(multiplexer_3_out[7]),
    .Output_0(Bits_are_inversed_here_output_0), .Output_1(Bits_are_inversed_here_output_1),
    .Output_2(Bits_are_inversed_here_output_2), .Output_3(Bits_are_inversed_here_output_3),
    .Output_4(Bits_are_inversed_here_output_4), .Output_5(Bits_are_inversed_here_output_5),
    .Output_6(Bits_are_inversed_here_output_6), .Output_7(Bits_are_inversed_here_output_7),
    .Zero(Bits_are_inversed_here_zero), .mult(main_5_mult), .add_sub(main_5_add_sub));  // open: Overflow
  Multiplexer #(.width(8)) multiplexer_5 (
    .in0(main_6_out_10), .in1(register_block_1_out_14), .out(multiplexer_5_out), .sel(main_3_out_16));  // open: en
  not not_4 (not_4_out, Bits_are_inversed_here_zero);
  and and_4 (and_4_out, main_1_out_17[0], main_3_branch, not_4_out);
  RAM8bits ram8bits_2 (
    .CLK(and_2_out), .in_2(main_1_out_17[5]), .ADDR(main_1_out_17[4]), .in_4(main_1_out_17[3]),
    .in_5(main_1_out_17[2]), .in_6(multiplexer_5_out[7]), .in_7(multiplexer_5_out[6]),
    .NIBBLE_1(multiplexer_5_out[5]), .in_9(multiplexer_5_out[4]), .in_10(multiplexer_5_out[3]),
    .NIBBLE_2(multiplexer_5_out[2]), .in_12(multiplexer_5_out[1]), .in_13(multiplexer_5_out[0]),
    .MODE(or_2_out), .out_15(ram8bits_2_out_22[7]), .out_16(ram8bits_2_out_22[6]),
    .out_17(ram8bits_2_out_22[5]), .out_18(ram8bits_2_out_22[4]), .out_19(ram8bits_2_out_22[3]),
    .out_20(ram8bits_2_out_22[2]), .out_21(ram8bits_2_out_22[1]), .out_22(ram8bits_2_out_22[0]));
  buf or_2 (or_2_out, main_3_out_16);  // OR_Gate
  _7_Segment_Display u_7_segment_display_1 (
    .g(main2_1_m_2[0]), .f(main2_1_m_2[1]), .a(main2_1_m_2[2]), .b(main2_1_m_2[3]), .e(main2_1_lb_2[0]),
    .d(main2_1_lb_2[1]), .c(main2_1_lb_2[2]));  // open: dp
  _7_Segment_Display u_7_segment_display_2 (
    .g(main2_1_m[0]), .f(main2_1_m[1]), .a(main2_1_m[2]), .b(main2_1_m[3]), .e(main2_1_lb[0]),
    .d(main2_1_lb[1]), .c(main2_1_lb[2]));  // open: dp
  IR_main main_7 (
    .INPUT(main_3_print), .Op2(register_block_1_out_14[7]), .Op1(register_block_1_out_14[6]),
    .Op0(register_block_1_out_14[5]), .Addr4(register_block_1_out_14[4]), .Addr3(register_block_1_out_14[3]),
    .Addr2(register_block_1_out_14[2]), .Addr1(register_block_1_out_14[1]),
    .Addr0(register_block_1_out_14[0]), .out_10(main_7_out_17[7]), .out_11(main_7_out_17[6]),
    .out_12(main_7_out_17[5]), .out_13(main_7_out_17[4]), .out_14(main_7_out_17[3]),
    .out_15(main_7_out_17[2]), .out_16(main_7_out_17[1]), .out_17(main_7_out_17[0]));
  main2 main2_1 (
    .M(main2_1_m[0]), .LT(main2_1_m[1]), .T(main2_1_m[2]), .RT(main2_1_m[3]), .LB(main2_1_lb[0]),
    .B(main2_1_lb[1]), .RB(main2_1_lb[2]), .M_2(main2_1_m_2[0]), .LT_2(main2_1_m_2[1]), .T_2(main2_1_m_2[2]),
    .RT_2(main2_1_m_2[3]), .LB_2(main2_1_lb_2[0]), .B_2(main2_1_lb_2[1]), .RB_2(main2_1_lb_2[2]),
    .in_1(main_7_out_17));

  // Notes on the sheet:
  //   IR
  //   KEY PAD
  //   INT
  //   Selecting branch or PC+1
  //   BetWeen buffer and data from CPU
  //   Branch equals 0
  //   CHOOSING between ALU and RAM
  //   BNZ
endmodule
